// Logisim project F3.circ as structural Verilog: 8 circuits, main circuit main
module main (
  input  in_1,
  input  in_2,
  input  in_3,
  input  in_4,
  input  in_5,
  input  in_6,
  input  in_7,
  input  in_8,
  input  in_9,
  output out_10,
  output out_11,
  output out_12,
  output out_13,
  output out_14,
  output out_15,
  output out_16,
  output out_17,
  output out_18,
  output out_19,
  output out_20,
  output out_21,
  output out_22,
  output out_23
);

  wire nand_1_out, nand_2_out, nand_3_out, nand_4_out, not_1_out, not_2_out, not_3_out, not_4_out;

  not not_1 (not_1_out, in_1);
  not not_2 (not_2_out, in_2);
  not not_3 (not_3_out, in_3);
  not not_4 (not_4_out, in_4);
  nand nand_1 (nand_1_out, not_1_out, in_2);
  nand nand_2 (nand_2_out, in_1, not_2_out);
  nand nand_3 (nand_3_out, not_3_out, not_4_out);
  nand nand_4 (nand_4_out, in_3, in_4);
  nand nand_5 (out_10, nand_1_out, nand_2_out);
  nand nand_6 (out_11, nand_3_out, nand_4_out);
  dec dec_1 (.A1(in_5), .A0(in_6), .Y3(out_12), .Y2(out_13), .Y1(out_14), .Y0(out_15));
  DEC8 dec8_1 (
    .A2(in_7), .A1(in_8), .A0(in_9), .Y7(out_16), .Y6(out_17), .Y5(out_18), .Y4(out_19), .Y3(out_20),
    .Y2(out_21), .Y1(out_22), .Y0(out_23));
endmodule

module dec (
  input  A1,
  input  A0,
  output Y3,
  output Y2,
  output Y1,
  output Y0
);

  wire not_1_out, not_2_out;

  not not_1 (not_1_out, A0);
  not not_2 (not_2_out, A1);
  and and_1 (Y3, A1, A0);
  and and_2 (Y2, not_1_out, A1);
  and and_3 (Y1, not_2_out, A0);
  and and_4 (Y0, not_2_out, not_1_out);
endmodule

module DEC8 (
  input  A2,
  input  A1,
  input  A0,
  output Y7,
  output Y6,
  output Y5,
  output Y4,
  output Y3,
  output Y2,
  output Y1,
  output Y0
);

  wire dec_1_y0, dec_1_y1, dec_1_y2, dec_1_y3, dec_2_y0, dec_2_y1, dec_2_y2, dec_2_y3, not_1_out;

  not not_1 (not_1_out, A2);
  dec dec_1 (.A1(A1), .A0(A0), .Y3(dec_1_y3), .Y2(dec_1_y2), .Y1(dec_1_y1), .Y0(dec_1_y0));
  dec dec_2 (.A1(A1), .A0(A0), .Y3(dec_2_y3), .Y2(dec_2_y2), .Y1(dec_2_y1), .Y0(dec_2_y0));
  and and_1 (Y7, A2, dec_1_y3);
  and and_2 (Y6, A2, dec_1_y2);
  and and_3 (Y5, A2, dec_1_y1);
  and and_4 (Y4, A2, dec_1_y0);
  and and_5 (Y3, dec_2_y3, not_1_out);
  and and_6 (Y2, dec_2_y2, not_1_out);
  and and_7 (Y1, dec_2_y1, not_1_out);
  and and_8 (Y0, dec_2_y0, not_1_out);
endmodule

module dec16 (
  input  A3,
  input  A2,
  input  A1,
  input  A0,
  output Y15,
  output Y14,
  output Y13,
  output Y12,
  output Y11,
  output Y10,
  output Y9,
  output Y8,
  output Y7,
  output Y6,
  output Y5,
  output Y4,
  output Y3,
  output Y2,
  output Y1,
  output Y0
);

  wire dec8_1_y0, dec8_1_y1, dec8_1_y2, dec8_1_y3, dec8_1_y4, dec8_1_y5, dec8_1_y6, dec8_1_y7, dec8_2_y0,
       dec8_2_y1, dec8_2_y2, dec8_2_y3, dec8_2_y4, dec8_2_y5, dec8_2_y6, dec8_2_y7, not_1_out;

  not not_1 (not_1_out, A3);
  DEC8 dec8_1 (
    .A2(A2), .A1(A1), .A0(A0), .Y7(dec8_1_y7), .Y6(dec8_1_y6), .Y5(dec8_1_y5), .Y4(dec8_1_y4),
    .Y3(dec8_1_y3), .Y2(dec8_1_y2), .Y1(dec8_1_y1), .Y0(dec8_1_y0));
  DEC8 dec8_2 (
    .A2(A2), .A1(A1), .A0(A0), .Y7(dec8_2_y7), .Y6(dec8_2_y6), .Y5(dec8_2_y5), .Y4(dec8_2_y4),
    .Y3(dec8_2_y3), .Y2(dec8_2_y2), .Y1(dec8_2_y1), .Y0(dec8_2_y0));
  and and_1 (Y15, A3, dec8_1_y7);
  and and_2 (Y14, A3, dec8_1_y6);
  and and_3 (Y13, A3, dec8_1_y5);
  and and_4 (Y12, A3, dec8_1_y4);
  and and_5 (Y11, A3, dec8_1_y3);
  and and_6 (Y10, A3, dec8_1_y2);
  and and_7 (Y9, A3, dec8_1_y1);
  and and_8 (Y8, A3, dec8_1_y0);
  and and_9 (Y7, not_1_out, dec8_2_y7);
  and and_10 (Y6, not_1_out, dec8_2_y6);
  and and_11 (Y5, not_1_out, dec8_2_y5);
  and and_12 (Y4, not_1_out, dec8_2_y4);
  and and_13 (Y3, not_1_out, dec8_2_y3);
  and and_14 (Y2, not_1_out, dec8_2_y2);
  and and_15 (Y1, not_1_out, dec8_2_y1);
  and and_16 (Y0, not_1_out, dec8_2_y0);
endmodule

module timer (
);

  wire and_1_out, and_2_out, and_3_out, and_4_out, and_5_out, and_6_out, and_7_out, and_8_out, and_9_out,
       and_10_out, and_11_out, and_12_out, and_13_out, and_14_out, and_15_out, and_16_out, and_17_out,
       and_18_out, and_19_out, and_20_out, and_21_out, and_22_out, and_23_out, and_24_out, and_25_out,
       and_26_out, and_27_out, and_28_out, clk_out, ledlight_1_a, ledlight_1_b, ledlight_1_c, ledlight_1_d,
       ledlight_1_e, ledlight_1_f, ledlight_1_g, ledlight_1_pointout, ledlight_2_a, ledlight_2_b,
       ledlight_2_c, ledlight_2_d, ledlight_2_e, ledlight_2_f, ledlight_2_g, ledlight_2_pointout,
       ledlight_3_a, ledlight_3_b, ledlight_3_c, ledlight_3_d, ledlight_3_e, ledlight_3_f, ledlight_3_g,
       ledlight_3_pointout, ledlight_4_a, ledlight_4_b, ledlight_4_c, ledlight_4_d, ledlight_4_e,
       ledlight_4_f, ledlight_4_g, ledlight_4_pointout, not_1_out, not_2_out, not_3_out, not_4_out,
       not_5_out, not_6_out, not_7_out, not_8_out, not_9_out, not_10_out, not_11_out, not_12_out, not_13_out,
       not_14_out, not_15_out, not_16_out, not_17_out, register_1_q, register_2_q, register_3_q;
  wire [3:0] cla4_1_s, cla4_2_s, cla4_3_s, cla4_4_s, register_4_q, register_5_q, register_6_q, register_7_q;

  Clock clk (.out(clk_out));
  and and_1 (and_1_out, and_18_out, and_3_out);
  Register #(.width(1)) register_1 (.D(and_3_out), .en(1'b1), .clk(clk_out), .Q(register_1_q), .clr(1'b0));
  Register #(.width(1)) register_2 (.D(and_1_out), .en(1'b1), .clk(clk_out), .Q(register_2_q), .clr(1'b0));
  Register #(.width(1)) register_3 (.D(and_2_out), .en(1'b1), .clk(clk_out), .Q(register_3_q), .clr(1'b0));
  Register #(.width(4)) register_4 (.D(cla4_2_s), .en(1'b1), .clk(clk_out), .Q(register_4_q), .clr(and_7_out));
  Register #(.width(4)) register_5 (.D(cla4_3_s), .en(register_1_q), .clk(clk_out), .Q(register_5_q), .clr(and_12_out));
  Register #(.width(4)) register_6 (.D(cla4_4_s), .en(register_2_q), .clk(clk_out), .Q(register_6_q), .clr(and_4_out));
  Register #(.width(4)) register_7 (.D(cla4_1_s), .en(register_3_q), .clk(clk_out), .Q(register_7_q), .clr(and_16_out));
  and and_2 (and_2_out, and_3_out, and_14_out);
  and and_3 (and_3_out, and_5_out, and_6_out);
  and and_4 (and_4_out, and_8_out, and_9_out);
  and and_5 (and_5_out, register_4_q[3], not_1_out);
  and and_6 (and_6_out, not_2_out, not_3_out);
  and and_7 (and_7_out, and_10_out, and_11_out);
  and and_8 (and_8_out, register_6_q[3], not_4_out);
  and and_9 (and_9_out, register_6_q[1], not_5_out);
  not not_1 (not_1_out, register_4_q[2]);
  not not_2 (not_2_out, register_4_q[1]);
  not not_3 (not_3_out, register_4_q[0]);
  and and_10 (and_10_out, register_4_q[3], not_6_out);
  and and_11 (and_11_out, register_4_q[1], not_7_out);
  and and_12 (and_12_out, and_7_out, and_17_out);
  not not_4 (not_4_out, register_6_q[2]);
  not not_5 (not_5_out, register_6_q[0]);
  and and_13 (and_13_out, and_19_out, and_20_out);
  and and_14 (and_14_out, and_13_out, and_15_out);
  and and_15 (and_15_out, and_21_out, and_22_out);
  and and_16 (and_16_out, and_23_out, and_24_out);
  not not_6 (not_6_out, register_4_q[2]);
  not not_7 (not_7_out, register_4_q[0]);
  and and_17 (and_17_out, and_25_out, and_26_out);
  and and_18 (and_18_out, and_27_out, and_28_out);
  CLA4 cla4_1 (.Cin(1'b0), .A(register_7_q), .B(4'b0001), .S(cla4_1_s));  // open: Cout
  and and_19 (and_19_out, register_6_q[3], not_10_out);
  and and_20 (and_20_out, not_11_out, register_6_q[0]);
  and and_21 (and_21_out, not_12_out, register_5_q[2]);
  and and_22 (and_22_out, not_13_out, register_5_q[0]);
  and and_23 (and_23_out, not_14_out, register_7_q[2]);
  and and_24 (and_24_out, register_7_q[1], not_15_out);
  CLA4 cla4_2 (.Cin(1'b0), .A(register_4_q), .B(4'b0001), .S(cla4_2_s));  // open: Cout
  CLA4 cla4_3 (.Cin(1'b0), .A(register_5_q), .B(4'b0001), .S(cla4_3_s));  // open: Cout
  not not_8 (not_8_out, register_5_q[3]);
  and and_25 (and_25_out, not_8_out, register_5_q[2]);
  and and_26 (and_26_out, register_5_q[1], not_9_out);
  not not_9 (not_9_out, register_5_q[0]);
  CLA4 cla4_4 (.Cin(1'b0), .A(register_6_q), .B(4'b0001), .S(cla4_4_s));  // open: Cout
  and and_27 (and_27_out, not_16_out, register_5_q[2]);
  and and_28 (and_28_out, not_17_out, register_5_q[0]);
  not not_10 (not_10_out, register_6_q[2]);
  not not_11 (not_11_out, register_6_q[1]);
  not not_12 (not_12_out, register_5_q[3]);
  not not_13 (not_13_out, register_5_q[1]);
  not not_14 (not_14_out, register_7_q[3]);
  not not_15 (not_15_out, register_7_q[0]);
  not not_16 (not_16_out, register_5_q[3]);
  not not_17 (not_17_out, register_5_q[1]);
  ledlight ledlight_1 (
    .A3(register_4_q[3]), .A2(register_4_q[2]), .A1(register_4_q[1]), .Pointin(1'b0), .A0(register_4_q[0]),
    .G(ledlight_1_g), .F(ledlight_1_f), .A(ledlight_1_a), .B(ledlight_1_b), .Pointout(ledlight_1_pointout),
    .C(ledlight_1_c), .D(ledlight_1_d), .E(ledlight_1_e));
  ledlight ledlight_2 (
    .A3(register_5_q[3]), .A2(register_5_q[2]), .A1(register_5_q[1]), .Pointin(1'b0), .A0(register_5_q[0]),
    .G(ledlight_2_g), .F(ledlight_2_f), .A(ledlight_2_a), .B(ledlight_2_b), .Pointout(ledlight_2_pointout),
    .C(ledlight_2_c), .D(ledlight_2_d), .E(ledlight_2_e));
  ledlight ledlight_3 (
    .A3(register_6_q[3]), .A2(register_6_q[2]), .A1(register_6_q[1]), .Pointin(1'b1), .A0(register_6_q[0]),
    .G(ledlight_3_g), .F(ledlight_3_f), .A(ledlight_3_a), .B(ledlight_3_b), .Pointout(ledlight_3_pointout),
    .C(ledlight_3_c), .D(ledlight_3_d), .E(ledlight_3_e));
  ledlight ledlight_4 (
    .A3(register_7_q[3]), .A2(register_7_q[2]), .A1(register_7_q[1]), .Pointin(1'b0), .A0(register_7_q[0]),
    .G(ledlight_4_g), .F(ledlight_4_f), .A(ledlight_4_a), .B(ledlight_4_b), .Pointout(ledlight_4_pointout),
    .C(ledlight_4_c), .D(ledlight_4_d), .E(ledlight_4_e));
  _7_Segment_Display u_7_segment_display_1 (
    .g(ledlight_2_g), .f(ledlight_2_f), .a(ledlight_2_a), .b(ledlight_2_b), .e(ledlight_2_e),
    .d(ledlight_2_d), .c(ledlight_2_c), .dp(ledlight_2_pointout));
  _7_Segment_Display u_7_segment_display_2 (
    .g(ledlight_1_g), .f(ledlight_1_f), .a(ledlight_1_a), .b(ledlight_1_b), .e(ledlight_1_e),
    .d(ledlight_1_d), .c(ledlight_1_c), .dp(ledlight_1_pointout));
  _7_Segment_Display u_7_segment_display_3 (
    .g(ledlight_4_g), .f(ledlight_4_f), .a(ledlight_4_a), .b(ledlight_4_b), .e(ledlight_4_e),
    .d(ledlight_4_d), .c(ledlight_4_c), .dp(ledlight_4_pointout));
  _7_Segment_Display u_7_segment_display_4 (
    .g(ledlight_3_g), .f(ledlight_3_f), .a(ledlight_3_a), .b(ledlight_3_b), .e(ledlight_3_e),
    .d(ledlight_3_d), .c(ledlight_3_c), .dp(ledlight_3_pointout));
endmodule

module FA (
  input  A,
  input  B,
  output Cout,
  output Sum
);

  wire and_2_out, and_3_out, not_1_out, not_2_out;

  not not_1 (not_1_out, A);
  not not_2 (not_2_out, B);
  and and_1 (Cout, A, B);
  and and_2 (and_2_out, not_1_out, B);
  and and_3 (and_3_out, A, not_2_out);
  or or_1 (Sum, and_2_out, and_3_out);
endmodule

module CLA4 (
  input  Cin,
  input  [3:0] A,
  input  [3:0] B,
  output [3:0] S,
  output Cout
);

  wire and_1_out, and_2_out, and_3_out, and_4_out, and_5_out, and_6_out, and_7_out, and_8_out, and_9_out,
       and_10_out, and_11_out, and_12_out, and_13_out, and_14_out, and_15_out, and_16_out, and_17_out,
       and_18_out, and_19_out, and_20_out, or_1_out, or_2_out, or_3_out, or_4_out, or_5_out, or_6_out,
       or_7_out, or_8_out, or_9_out, or_10_out, or_11_out, or_12_out, or_13_out, or_14_out, or_15_out,
       or_16_out, or_17_out, or_18_out, or_19_out, xor_1_out, xor_3_out, xor_5_out, xor_7_out;

  xor xor_1 (xor_1_out, A[0], B[0]);
  and and_1 (and_1_out, A[0], B[0]);
  or or_1 (or_1_out, A[0], B[0]);
  and and_2 (and_2_out, A[0], B[0]);
  or or_2 (or_2_out, A[0], B[0]);
  and and_3 (and_3_out, A[0], B[0]);
  or or_3 (or_3_out, A[0], B[0]);
  and and_4 (and_4_out, A[0], B[0]);
  or or_4 (or_4_out, A[0], B[0]);
  xor xor_2 (S[0], Cin, xor_1_out);
  or or_5 (or_5_out, and_1_out, and_5_out);
  and and_5 (and_5_out, or_1_out, Cin);
  or or_6 (or_6_out, and_2_out, and_6_out);
  and and_6 (and_6_out, or_2_out, Cin);
  or or_7 (or_7_out, A[1], B[1]);
  and and_7 (and_7_out, A[1], B[1]);
  or or_8 (or_8_out, and_3_out, and_8_out);
  and and_8 (and_8_out, or_3_out, Cin);
  or or_9 (or_9_out, A[1], B[1]);
  and and_9 (and_9_out, A[1], B[1]);
  or or_10 (or_10_out, A[2], B[2]);
  and and_10 (and_10_out, A[2], B[2]);
  or or_11 (or_11_out, and_4_out, and_11_out);
  and and_11 (and_11_out, or_4_out, Cin);
  or or_12 (or_12_out, A[1], B[1]);
  and and_12 (and_12_out, A[1], B[1]);
  or or_13 (or_13_out, A[2], B[2]);
  and and_13 (and_13_out, A[2], B[2]);
  or or_14 (or_14_out, A[3], B[3]);
  and and_14 (and_14_out, A[3], B[3]);
  xor xor_3 (xor_3_out, or_5_out, A[1]);
  and and_15 (and_15_out, or_6_out, or_7_out);
  and and_16 (and_16_out, or_8_out, or_9_out);
  and and_17 (and_17_out, or_11_out, or_12_out);
  xor xor_4 (S[1], xor_3_out, B[1]);
  or or_15 (or_15_out, and_15_out, and_7_out);
  or or_16 (or_16_out, and_16_out, and_9_out);
  or or_17 (or_17_out, and_17_out, and_12_out);
  xor xor_5 (xor_5_out, or_15_out, A[2]);
  and and_18 (and_18_out, or_16_out, or_10_out);
  or or_18 (or_18_out, and_18_out, and_10_out);
  and and_19 (and_19_out, or_17_out, or_13_out);
  or or_19 (or_19_out, and_19_out, and_13_out);
  xor xor_6 (S[2], xor_5_out, B[2]);
  xor xor_7 (xor_7_out, or_18_out, A[3]);
  and and_20 (and_20_out, or_19_out, or_14_out);
  xor xor_8 (S[3], xor_7_out, B[3]);
  or or_20 (Cout, and_20_out, and_14_out);
endmodule

module ledlight (
  input  A3,
  input  A2,
  input  A1,
  input  Pointin,
  input  A0,
  output G,
  output F,
  output A,
  output B,
  output Pointout,
  output C,
  output D,
  output E
);

  wire dec16_1_y0, dec16_1_y1, dec16_1_y2, dec16_1_y3, dec16_1_y4, dec16_1_y5, dec16_1_y6, dec16_1_y7,
       dec16_1_y8, dec16_1_y9, dec16_1_y10, dec16_1_y11, dec16_1_y12, dec16_1_y13, dec16_1_y14, dec16_1_y15,
       or_1_out, or_2_out, or_3_out, or_4_out, or_5_out, or_6_out, or_7_out, or_8_out, or_9_out, or_10_out,
       or_11_out, or_12_out, or_13_out, or_14_out, or_15_out, or_16_out, or_17_out, or_18_out, or_19_out,
       or_20_out, or_21_out, or_22_out, or_23_out, or_24_out, or_25_out, or_26_out, or_27_out, or_28_out,
       or_29_out, or_30_out, or_31_out, or_32_out, or_33_out, or_34_out, or_35_out, or_36_out, or_37_out,
       or_38_out, or_39_out, or_40_out, or_41_out, or_42_out, or_43_out, or_44_out, or_45_out, or_46_out,
       or_47_out, or_48_out, or_49_out, or_50_out, or_51_out, or_52_out, or_53_out, or_54_out, or_55_out,
       or_56_out, or_57_out, or_58_out, or_59_out, or_60_out, or_63_out, or_64_out, or_68_out, or_70_out;

  dec16 dec16_1 (
    .A3(A3), .A2(A2), .A1(A1), .A0(A0), .Y15(dec16_1_y15), .Y14(dec16_1_y14), .Y13(dec16_1_y13),
    .Y12(dec16_1_y12), .Y11(dec16_1_y11), .Y10(dec16_1_y10), .Y9(dec16_1_y9), .Y8(dec16_1_y8),
    .Y7(dec16_1_y7), .Y6(dec16_1_y6), .Y5(dec16_1_y5), .Y4(dec16_1_y4), .Y3(dec16_1_y3), .Y2(dec16_1_y2),
    .Y1(dec16_1_y1), .Y0(dec16_1_y0));
  or or_1 (or_1_out, dec16_1_y9, dec16_1_y8);
  or or_2 (or_2_out, or_1_out, or_3_out);
  or or_3 (or_3_out, dec16_1_y7, dec16_1_y4);
  or or_4 (or_4_out, dec16_1_y3, dec16_1_y2);
  or or_5 (or_5_out, or_4_out, or_6_out);
  or or_6 (or_6_out, dec16_1_y1, dec16_1_y0);
  or or_7 (or_7_out, dec16_1_y0, dec16_1_y2);
  or or_8 (or_8_out, or_7_out, or_9_out);
  or or_9 (or_9_out, dec16_1_y3, dec16_1_y5);
  or or_10 (or_10_out, dec16_1_y6, dec16_1_y7);
  or or_11 (or_11_out, or_10_out, or_12_out);
  or or_12 (or_12_out, dec16_1_y8, dec16_1_y9);
  or or_13 (or_13_out, dec16_1_y0, dec16_1_y1);
  or or_14 (or_14_out, or_13_out, or_15_out);
  or or_15 (or_15_out, dec16_1_y3, dec16_1_y4);
  or or_16 (or_16_out, dec16_1_y5, dec16_1_y6);
  or or_17 (or_17_out, or_16_out, or_18_out);
  or or_18 (or_18_out, dec16_1_y7, dec16_1_y8);
  or or_19 (or_19_out, dec16_1_y0, dec16_1_y2);
  or or_20 (or_20_out, or_19_out, or_21_out);
  or or_21 (or_21_out, dec16_1_y3, dec16_1_y5);
  or or_22 (or_22_out, dec16_1_y6, dec16_1_y8);
  or or_23 (or_23_out, dec16_1_y0, dec16_1_y2);
  or or_24 (or_24_out, or_23_out, or_25_out);
  or or_25 (or_25_out, dec16_1_y6, dec16_1_y8);
  or or_26 (or_26_out, dec16_1_y0, dec16_1_y4);
  or or_27 (or_27_out, or_26_out, or_28_out);
  or or_28 (or_28_out, dec16_1_y5, dec16_1_y6);
  or or_29 (or_29_out, dec16_1_y8, dec16_1_y9);
  or or_30 (or_30_out, dec16_1_y2, dec16_1_y3);
  or or_31 (or_31_out, or_30_out, or_32_out);
  or or_32 (or_32_out, dec16_1_y4, dec16_1_y5);
  or or_33 (or_33_out, dec16_1_y6, dec16_1_y8);
  or or_34 (or_34_out, or_33_out, dec16_1_y9);
  or or_35 (or_35_out, dec16_1_y15, dec16_1_y14);
  or or_36 (or_36_out, dec16_1_y13, dec16_1_y11);
  or or_37 (or_37_out, dec16_1_y10, or_54_out);
  or or_38 (or_38_out, dec16_1_y15, dec16_1_y14);
  or or_39 (or_39_out, dec16_1_y12, dec16_1_y11);
  or or_40 (or_40_out, dec16_1_y10, or_53_out);
  or or_41 (or_41_out, dec16_1_y15, dec16_1_y14);
  or or_42 (or_42_out, dec16_1_y13, dec16_1_y12);
  or or_43 (or_43_out, dec16_1_y11, dec16_1_y10);
  or or_44 (or_44_out, dec16_1_y14, dec16_1_y13);
  or or_45 (or_45_out, dec16_1_y12, dec16_1_y11);
  _7_Segment_Display u_7_segment_display_1 (.g(G), .f(F), .a(A), .b(B), .e(E), .d(D), .c(C), .dp(Pointin));
  or or_46 (or_46_out, dec16_1_y15, dec16_1_y14);
  or or_47 (or_47_out, dec16_1_y12, dec16_1_y10);
  or or_48 (or_48_out, dec16_1_y10, dec16_1_y13);
  or or_49 (or_49_out, or_2_out, or_5_out);
  or or_50 (or_50_out, or_8_out, or_11_out);
  or or_51 (or_51_out, or_14_out, or_17_out);
  or or_52 (or_52_out, or_20_out, or_22_out);
  or or_53 (or_53_out, or_27_out, or_29_out);
  or or_54 (or_54_out, or_31_out, or_34_out);
  or or_55 (or_55_out, or_35_out, or_36_out);
  or or_56 (or_56_out, or_38_out, or_39_out);
  or or_57 (or_57_out, or_41_out, or_42_out);
  or or_58 (or_58_out, or_24_out, or_43_out);
  or or_59 (or_59_out, or_44_out, or_45_out);
  or or_60 (or_60_out, or_46_out, or_47_out);
  or or_61 (A, or_60_out, or_50_out);
  or or_62 (B, or_48_out, or_49_out);
  or or_63 (or_63_out, dec16_1_y11, dec16_1_y10);
  or or_64 (or_64_out, or_51_out, dec16_1_y9);
  or or_65 (G, or_55_out, or_37_out);
  or or_66 (F, or_56_out, or_40_out);
  or or_67 (E, or_57_out, or_58_out);
  or or_68 (or_68_out, or_59_out, or_52_out);
  or or_69 (C, dec16_1_y13, or_70_out);
  or or_70 (or_70_out, or_63_out, or_64_out);
  or or_71 (D, or_68_out, dec16_1_y9);

  assign Pointout = Pointin;
endmodule
