// Logisim project F5.circ as structural Verilog
module RomByMux (
  input  [3:0] PC,
  output [7:0] OPN
);

  Multiplexer #(.select(4), .width(8)) multiplexer_1 (
    .in0(8'h8a), .in1(8'h90), .in2(8'ha0), .in3(8'hb1), .in4(8'h17), .in5(8'h29), .in6(8'hd1), .in7(8'hdf),
    .out(OPN), .sel(PC));  // open: in8, in9, in10, in11, in12, in13, in14, in15
endmodule

module RamByReg (
  input  [1:0] addr,
  input  [7:0] D,
  input  WriteEN,
  input  [1:0] Read1,
  input  [1:0] Read2,
  input  [1:0] Read3,
  output [7:0] Q,
  output [7:0] Out1,
  output [7:0] Out2,
  output [7:0] Out3,
  output [7:0] OUT_R3,
  output [7:0] OUT_R2,
  output [7:0] OUT_R1,
  output [7:0] OUT_R0
);

  wire and_1_out, and_4_out, and_9_out, and_16_out, clk_out;
  wire [7:0] and_2_out, and_3_out, and_5_out, and_6_out, and_7_out, and_8_out, and_10_out, and_11_out,
       and_12_out, and_13_out, and_14_out, and_15_out, and_17_out, and_18_out, and_19_out, and_20_out,
       and_21_out, and_22_out, and_23_out, and_24_out;
  wire [7:7] decoder_1_out0, decoder_1_out1, decoder_1_out2, decoder_1_out3, decoder_2_out0, decoder_2_out1,
       decoder_2_out2, decoder_2_out3, decoder_3_out0, decoder_3_out1, decoder_3_out2, decoder_3_out3,
       decoder_4_out0, decoder_4_out1, decoder_4_out2, decoder_4_out3;

  Decoder #(.select(2)) decoder_1 (
    .out0(decoder_1_out0[7]), .out1(decoder_1_out1[7]), .out2(decoder_1_out2[7]), .out3(decoder_1_out3[7]),
    .sel(addr), .en(1'b1));
  Decoder #(.enable("false"), .select(2)) decoder_2 (
    .out0(decoder_2_out0[7]), .out1(decoder_2_out1[7]), .out2(decoder_2_out2[7]), .out3(decoder_2_out3[7]),
    .sel(Read1));
  Decoder #(.enable("false"), .select(2)) decoder_3 (
    .out0(decoder_3_out0[7]), .out1(decoder_3_out1[7]), .out2(decoder_3_out2[7]), .out3(decoder_3_out3[7]),
    .sel(Read2));
  Decoder #(.enable("false"), .select(2)) decoder_4 (
    .out0(decoder_4_out0[7]), .out1(decoder_4_out1[7]), .out2(decoder_4_out2[7]), .out3(decoder_4_out3[7]),
    .sel(Read3));
  Clock clk (.out(clk_out));
  and and_1 (and_1_out, WriteEN, decoder_1_out0[7]);
  assign and_2_out = {8{decoder_1_out0[7]}} & D;  // AND_Gate and_2, 8 bits wide
  Register R0 (.D(and_2_out), .en(and_1_out), .clk(clk_out), .Q(OUT_R0), .clr(1'b0));
  assign and_3_out = {8{decoder_1_out1[7]}} & D;  // AND_Gate and_3, 8 bits wide
  and and_4 (and_4_out, WriteEN, decoder_1_out1[7]);
  assign and_5_out = {8{decoder_2_out0[7]}} & OUT_R0;  // AND_Gate and_5, 8 bits wide
  assign and_6_out = {8{decoder_1_out0[7]}} & OUT_R0;  // AND_Gate and_6, 8 bits wide
  assign and_7_out = {8{decoder_3_out0[7]}} & OUT_R0;  // AND_Gate and_7, 8 bits wide
  assign and_8_out = {8{decoder_4_out0[7]}} & OUT_R0;  // AND_Gate and_8, 8 bits wide
  Register R1 (.D(and_3_out), .en(and_4_out), .clk(clk_out), .Q(OUT_R1), .clr(1'b0));
  and and_9 (and_9_out, WriteEN, decoder_1_out2[7]);
  assign and_10_out = {8{decoder_1_out2[7]}} & D;  // AND_Gate and_10, 8 bits wide
  Register R2 (.D(and_10_out), .en(and_9_out), .clk(clk_out), .Q(OUT_R2), .clr(1'b0));
  assign and_11_out = {8{decoder_1_out3[7]}} & D;  // AND_Gate and_11, 8 bits wide
  assign and_12_out = {8{decoder_2_out1[7]}} & OUT_R1;  // AND_Gate and_12, 8 bits wide
  assign and_13_out = {8{decoder_1_out1[7]}} & OUT_R1;  // AND_Gate and_13, 8 bits wide
  assign and_14_out = {8{decoder_3_out1[7]}} & OUT_R1;  // AND_Gate and_14, 8 bits wide
  assign and_15_out = {8{decoder_4_out1[7]}} & OUT_R1;  // AND_Gate and_15, 8 bits wide
  and and_16 (and_16_out, WriteEN, decoder_1_out3[7]);
  assign and_17_out = {8{decoder_2_out2[7]}} & OUT_R2;  // AND_Gate and_17, 8 bits wide
  assign and_18_out = {8{decoder_3_out2[7]}} & OUT_R2;  // AND_Gate and_18, 8 bits wide
  assign and_19_out = {8{decoder_4_out2[7]}} & OUT_R2;  // AND_Gate and_19, 8 bits wide
  Register R3 (.D(and_11_out), .en(and_16_out), .clk(clk_out), .Q(OUT_R3), .clr(1'b0));
  assign and_20_out = {8{decoder_1_out2[7]}} & OUT_R2;  // AND_Gate and_20, 8 bits wide
  assign Out1 = and_12_out | and_5_out | and_17_out | and_21_out;  // OR_Gate or_1, 8 bits wide
  assign and_21_out = OUT_R3 & {8{decoder_2_out3[7]}};  // AND_Gate and_21, 8 bits wide
  assign and_22_out = {8{decoder_1_out3[7]}} & OUT_R3;  // AND_Gate and_22, 8 bits wide
  assign Q = and_22_out | and_20_out | and_13_out | and_6_out;  // OR_Gate or_2, 8 bits wide
  assign Out2 = and_7_out | and_14_out | and_18_out | and_23_out;  // OR_Gate or_3, 8 bits wide
  assign and_23_out = {8{decoder_3_out3[7]}} & OUT_R3;  // AND_Gate and_23, 8 bits wide
  assign Out3 = and_8_out | and_15_out | and_19_out | and_24_out;  // OR_Gate or_4, 8 bits wide
  assign and_24_out = {8{decoder_4_out3[7]}} & OUT_R3;  // AND_Gate and_24, 8 bits wide
endmodule

module PC (
  input  [3:0] PCin,
  input  PCin_EN,
  input  reset,
  output [7:0] OPN
);

  wire and_1_out, and_2_out, and_3_out, CLK_out, not_1_out, not_2_out, not_3_out;
  wire [3:0] and_4_out, and_5_out, fa_1_sum, multiplexer_1_out, not_4_out, or_1_out, register_1_q;

  and and_1 (and_1_out, not_1_out, not_2_out);
  and and_2 (and_2_out, and_1_out, and_3_out);
  and and_3 (and_3_out, not_3_out, register_1_q[3]);
  not not_1 (not_1_out, register_1_q[0]);
  not not_2 (not_2_out, register_1_q[1]);
  not not_3 (not_3_out, register_1_q[2]);
  Multiplexer #(.width(4)) multiplexer_1 (.in0(or_1_out), .in1(4'b0000), .out(multiplexer_1_out), .sel(reset));
  Clock CLK (.out(CLK_out));
  Register #(.width(4)) register_1 (.D(multiplexer_1_out), .en(1'b1), .clk(CLK_out), .Q(register_1_q), .clr(and_2_out));
  assign or_1_out = and_4_out | and_5_out;  // OR_Gate or_1, 4 bits wide
  assign and_4_out = PCin & {4{PCin_EN}};  // AND_Gate and_4, 4 bits wide
  assign and_5_out = not_4_out & fa_1_sum;  // AND_Gate and_5, 4 bits wide
  assign not_4_out = ~{4{PCin_EN}};  // NOT_Gate not_4, 4 bits wide
  RomByMux rombymux_1 (.PC(register_1_q), .OPN(OPN));
  FA fa_1 (.Cin(1'b0), .A(register_1_q), .B(4'b0001), .Sum(fa_1_sum));  // open: Cout
endmodule

module FA (
  input  Cin,
  input  [3:0] A,
  input  [3:0] B,
  output [3:0] Sum,
  output Cout
);

  wire and_1_out, and_2_out, and_3_out, and_4_out, and_5_out, and_6_out, and_7_out, and_8_out, or_1_out,
       or_2_out, or_3_out, or_4_out, or_5_out, or_6_out, or_7_out, xor_1_out, xor_3_out, xor_5_out, xor_7_out;

  or or_1 (or_1_out, A[0], B[0]);
  and and_1 (and_1_out, Cin, or_1_out);
  and and_2 (and_2_out, A[0], B[0]);
  or or_2 (or_2_out, A[1], B[1]);
  and and_3 (and_3_out, A[1], B[1]);
  xor xor_1 (xor_1_out, Cin, A[0]);
  or or_3 (or_3_out, and_1_out, and_2_out);
  or or_4 (or_4_out, A[2], B[2]);
  and and_4 (and_4_out, A[2], B[2]);
  or or_5 (or_5_out, A[3], B[3]);
  and and_5 (and_5_out, A[3], B[3]);
  xor xor_2 (Sum[0], xor_1_out, B[0]);
  xor xor_3 (xor_3_out, or_3_out, A[1]);
  xor xor_4 (Sum[1], xor_3_out, B[1]);
  and and_6 (and_6_out, or_3_out, or_2_out);
  or or_6 (or_6_out, and_6_out, and_3_out);
  xor xor_5 (xor_5_out, or_6_out, A[2]);
  xor xor_6 (Sum[2], xor_5_out, B[2]);
  and and_7 (and_7_out, or_6_out, or_4_out);
  or or_7 (or_7_out, and_7_out, and_4_out);
  xor xor_7 (xor_7_out, or_7_out, A[3]);
  and and_8 (and_8_out, or_7_out, or_5_out);
  xor xor_8 (Sum[3], xor_7_out, B[3]);
  or or_8 (Cout, and_8_out, and_5_out);
endmodule

module sCPU (
  output [7:0] R3,
  output [7:0] R2,
  output [7:0] OUT_OPN,
  output [7:0] R1,
  output [7:0] R0
);

  wire and_1_out, and_2_out, and_3_out, comparator_1_gt, comparator_1_lt, fa_1_cout, nor_1_out, not_1_out,
       or_1_out, or_2_out;
  wire [3:0] fa_1_sum, fa_2_sum;
  wire [7:0] multiplexer_1_out, rambyreg_1_out1, rambyreg_1_out2, rambyreg_1_out3;

  PC pc_1 (.PCin(OUT_OPN[5:2]), .PCin_EN(and_3_out), .OPN(OUT_OPN));  // open: reset
  not not_1 (not_1_out, OUT_OPN[6]);
  Multiplexer #(.select(2), .width(8)) multiplexer_1 (
    .in0({fa_2_sum, fa_1_sum}), .in2({4'b0000, OUT_OPN[3:0]}), .out(multiplexer_1_out), .sel(OUT_OPN[7:6]));  // open: in1, in3
  and and_1 (and_1_out, not_1_out, OUT_OPN[7]);
  nor nor_1 (nor_1_out, OUT_OPN[6], OUT_OPN[7]);
  and and_2 (and_2_out, OUT_OPN[6], OUT_OPN[7]);
  and and_3 (and_3_out, and_2_out, or_2_out);
  or or_1 (or_1_out, and_1_out, nor_1_out);
  RamByReg rambyreg_1 (
    .addr(OUT_OPN[5:4]), .D(multiplexer_1_out), .WriteEN(or_1_out), .Read1(OUT_OPN[3:2]),
    .Read2(OUT_OPN[1:0]), .Read3(2'b00), .Out1(rambyreg_1_out1), .Out2(rambyreg_1_out2),
    .Out3(rambyreg_1_out3), .OUT_R3(R3), .OUT_R2(R2), .OUT_R1(R1), .OUT_R0(R0));  // open: Q
  Comparator comparator_1 (
    .a(rambyreg_1_out2), .b(rambyreg_1_out3), .gt(comparator_1_gt), .lt(comparator_1_lt));  // open: eq
  or or_2 (or_2_out, comparator_1_lt, comparator_1_gt);
  FA fa_1 (.Cin(1'b0), .A(rambyreg_1_out1[3:0]), .B(rambyreg_1_out2[3:0]), .Sum(fa_1_sum), .Cout(fa_1_cout));
  FA fa_2 (.Cin(fa_1_cout), .A(rambyreg_1_out1[7:4]), .B(rambyreg_1_out2[7:4]), .Sum(fa_2_sum));  // open: Cout
endmodule

module sCPU_2 (
  input  [7:0] OPN,
  output [7:0] R3,
  output [7:0] R2,
  output [7:0] OUT_OPN,
  output [7:0] R1,
  output [7:0] R0
);

  wire and_1_out, and_2_out, and_3_out, comparator_1_gt, comparator_1_lt, fa_1_cout, nor_1_out, not_1_out,
       or_1_out, or_2_out;
  wire [3:0] fa_1_sum, fa_2_sum, rambyreg_1_out1, rambyreg_1_out1_2, rambyreg_1_out2, rambyreg_1_out2_2;
  wire [7:0] multiplexer_1_out, rambyreg_1_out3;

  PC_2 pc_2_1 (.PCin(OUT_OPN[5:2]), .PCin_EN(and_3_out), .OPN(OUT_OPN));  // open: reset
  Multiplexer #(.select(2), .width(8)) multiplexer_1 (
    .in0({fa_2_sum, fa_1_sum}), .in2({4'b0000, OUT_OPN[3:0]}), .out(multiplexer_1_out), .sel(OUT_OPN[7:6]));  // open: in1, in3
  not not_1 (not_1_out, OUT_OPN[6]);
  and and_1 (and_1_out, not_1_out, OUT_OPN[7]);
  nor nor_1 (nor_1_out, OUT_OPN[6], OUT_OPN[7]);
  and and_2 (and_2_out, OUT_OPN[6], OUT_OPN[7]);
  and and_3 (and_3_out, and_2_out, or_2_out);
  or or_1 (or_1_out, and_1_out, nor_1_out);
  RamByReg rambyreg_1 (
    .addr(OUT_OPN[5:4]), .D(multiplexer_1_out), .WriteEN(or_1_out), .Read1(OUT_OPN[3:2]),
    .Read2(OUT_OPN[1:0]), .Read3(2'b00), .Out1({rambyreg_1_out1_2, rambyreg_1_out1}),
    .Out2({rambyreg_1_out2_2, rambyreg_1_out2}), .Out3(rambyreg_1_out3), .OUT_R3(R3), .OUT_R2(R2),
    .OUT_R1(R1), .OUT_R0(R0));  // open: Q
  or or_2 (or_2_out, comparator_1_lt, comparator_1_gt);
  Comparator comparator_1 (
    .a({rambyreg_1_out2_2, rambyreg_1_out2}), .b(rambyreg_1_out3), .gt(comparator_1_gt), .lt(comparator_1_lt));  // open: eq
  FA fa_1 (.Cin(1'b0), .A(rambyreg_1_out1), .B(rambyreg_1_out2), .Sum(fa_1_sum), .Cout(fa_1_cout));
  FA fa_2 (.Cin(fa_1_cout), .A(rambyreg_1_out1_2), .B(rambyreg_1_out2_2), .Sum(fa_2_sum));  // open: Cout
endmodule

module RomByMux_2 (
  input  [3:0] PC,
  output [7:0] OPN
);

  Multiplexer #(.select(4), .width(8)) multiplexer_1 (
    .in0(8'h89), .in1(8'h91), .in2(8'ha1), .in3(8'hb2), .in4(8'h17), .in5(8'h29), .in6(8'hd1), .in7(8'hdf),
    .out(OPN), .sel(PC));  // open: in8, in9, in10, in11, in12, in13, in14, in15
endmodule

module PC_2 (
  input  [3:0] PCin,
  input  PCin_EN,
  input  reset,
  output [7:0] OPN
);

  wire and_1_out, and_2_out, and_3_out, CLK_out, not_1_out, not_2_out, not_3_out;
  wire [3:0] and_4_out, and_5_out, fa_1_sum, multiplexer_1_out, not_4_out, or_1_out, register_1_q;

  and and_1 (and_1_out, not_1_out, not_2_out);
  and and_2 (and_2_out, and_1_out, and_3_out);
  and and_3 (and_3_out, not_3_out, register_1_q[3]);
  not not_1 (not_1_out, register_1_q[0]);
  not not_2 (not_2_out, register_1_q[1]);
  not not_3 (not_3_out, register_1_q[2]);
  Multiplexer #(.width(4)) multiplexer_1 (.in0(or_1_out), .in1(4'b0000), .out(multiplexer_1_out), .sel(reset));
  Clock CLK (.out(CLK_out));
  Register #(.width(4)) register_1 (.D(multiplexer_1_out), .en(1'b1), .clk(CLK_out), .Q(register_1_q), .clr(and_2_out));
  assign or_1_out = and_4_out | and_5_out;  // OR_Gate or_1, 4 bits wide
  assign and_4_out = PCin & {4{PCin_EN}};  // AND_Gate and_4, 4 bits wide
  assign and_5_out = not_4_out & fa_1_sum;  // AND_Gate and_5, 4 bits wide
  assign not_4_out = ~{4{PCin_EN}};  // NOT_Gate not_4, 4 bits wide
  RomByMux_2 rombymux_2_1 (.PC(register_1_q), .OPN(OPN));
  FA fa_1 (.Cin(1'b0), .A(register_1_q), .B(4'b0001), .Sum(fa_1_sum));  // open: Cout
endmodule
