// Logisim project F6.circ as structural Verilog: 5 circuits, main circuit main
module main (
  output [31:0] Command,
  output [31:0] PC,
  output [4:0] out_3,
  output [23:0] out_4,
  output [31:0] out_5,
  output [31:0] out_6,
  output [31:0] out_7,
  output [2:0] out_8,
  output [31:0] out_9,
  output [31:0] out_10,
  output [31:0] out_11
);

  wire and_1_out, and_2_out, BE0, BE1, BE2, BE3, CLK, comparator_1_eq, comparator_2_eq, comparator_3_eq,
       comparator_4_eq, comparator_5_eq, comparator_6_eq, comparator_7_eq, comparator_8_eq, comparator_9_eq,
       comparator_10_eq, comparator_11_eq, comparator_11_gt, comparator_12_eq, comparator_12_lt,
       comparator_14_eq, comparator_15_eq, comparator_16_eq, comparator_17_eq, comparator_18_eq,
       decoder_1_out0, decoder_1_out1, decoder_1_out2, decoder_1_out3, isRGB, not_2_out, or_1_out, or_2_out,
       or_3_out, or_4_out, or_5_out, or_6_out, or_7_out, or_8_out, rgb_video_1_p2, STOP;
  wire [1:0] RAM_Byte_SEL;
  wire [7:0] Byte0, Byte1, Byte2, Byte3, LBU_Result;
  wire [15:0] adder_2_out, register_1_q;
  wire [23:0] rgb_video_1_p5;
  wire [31:0] ADDI_Result, ALU_Result, imm, Plus4, write_data;
  wire [31:26] RGB_Address_Ensure;

  // NOT_Gate not_1 has open pins: in=STOP, out=open
  Clock clock_1 (.out(CLK));
  Comparator #(.width(3)) comparator_1 (.a(out_8), .b(3'b000), .eq(comparator_1_eq));  // open: gt, lt
  or or_1 (or_1_out, comparator_1_eq, comparator_2_eq);
  Comparator #(.width(3)) comparator_2 (.a(out_8), .b(3'b001), .eq(comparator_2_eq));  // open: gt, lt
  Comparator #(.width(3)) comparator_3 (.a(out_8), .b(3'b010), .eq(comparator_3_eq));  // open: gt, lt
  or or_2 (or_2_out, comparator_3_eq, comparator_4_eq);
  Comparator #(.width(3)) comparator_4 (.a(out_8), .b(3'b011), .eq(comparator_4_eq));  // open: gt, lt
  Comparator #(.width(3)) comparator_5 (.a(out_8), .b(3'b100), .eq(comparator_5_eq));  // open: gt, lt
  or or_3 (or_3_out, comparator_5_eq, comparator_6_eq);
  Comparator #(.width(3)) comparator_6 (.a(out_8), .b(3'b101), .eq(comparator_6_eq));  // open: gt, lt
  or or_4 (or_4_out, or_1_out, or_2_out, or_3_out);
  ROM #(.addrWidth(20), .dataWidth(32)) rom_1 (.addr(PC[21:2]), .data(Command));
  ProgramCounter programcounter_1 (.Op(out_8), .PC_input(ALU_Result), .clk(CLK), .CurrentPC(PC));  // open: NextPC
  GPR gpr_1 (
    .rs1_addr(Command[19:15]), .clk(CLK), .wdata(write_data), .rd_address(Command[11:7]), .WE(or_4_out),
    .rs2_addr(Command[24:20]), .rs1_val(out_10), .rs2_val(out_7));  // open: reset
  ALU alu_1 (.A(imm), .B(out_10), .Sum(ALU_Result));
  ALU alu_2 (.A(out_10), .B(out_7), .Sum(ADDI_Result));
  ALU alu_3 (.A(out_6), .B(out_10), .Sum(out_9));
  assign imm = {{20{Command[31]}}, Command[31:20]};  // Bit_Extender bit_extender_1
  Adder #(.width(32)) adder_1 (.a(PC), .b(32'h4), .out(Plus4));  // open: cin, cout
  Multiplexer #(.select(3), .width(32)) multiplexer_1 (
    .in4(ALU_Result), .in5(ALU_Result), .in6(out_9), .in7(out_9),
    .out({RGB_Address_Ensure, out_4, RAM_Byte_SEL}), .sel(out_8));  // open: in0, in1, in2, in3
  OpCoder opcoder_1 (.funct7(Command[31:25]), .OpCode(Command[6:0]), .funct3(Command[14:12]), .op(out_8));
  Register #(.width(16)) register_1 (.D(adder_2_out), .en(1'b1), .clk(CLK), .Q(register_1_q));  // open: clr
  Multiplexer #(.select(3), .width(32)) multiplexer_2 (
    .in0(ALU_Result), .in1(Plus4), .in2(ADDI_Result), .in3({Command[31:12], {12{1'b0}}}),
    .in4({Byte3, Byte2, Byte1, Byte0}), .in5({{24{1'b0}}, LBU_Result}), .out(write_data), .sel(out_8));  // open: in6, in7
  not not_2 (not_2_out, isRGB);
  Comparator #(.width(3)) comparator_7 (.a(out_8), .b(3'b100), .eq(comparator_7_eq));  // open: gt, lt
  Comparator #(.width(3)) comparator_8 (.a(out_8), .b(3'b101), .eq(comparator_8_eq));  // open: gt, lt
  Comparator #(.width(3)) comparator_9 (.a(out_8), .b(3'b110), .eq(comparator_9_eq));  // open: gt, lt
  Comparator #(.width(3)) comparator_10 (.a(out_8), .b(3'b111), .eq(comparator_10_eq));  // open: gt, lt
  Multiplexer #(.select(3), .width(32)) multiplexer_3 (
    .in6(out_7), .in7({out_7[7:0], out_7[7:0], out_7[7:0], out_7[7:0]}), .out(out_5), .sel(out_8));  // open: in0, in1, in2, in3, in4, in5
  Adder #(.width(16)) adder_2 (.a(register_1_q), .b(16'h1), .out(adder_2_out));  // open: cin, cout
  or or_5 (or_5_out, comparator_7_eq, comparator_8_eq);
  or or_6 (or_6_out, comparator_9_eq, comparator_10_eq);
  Comparator #(.width(32)) comparator_11 (
    .a({RGB_Address_Ensure, out_4, RAM_Byte_SEL}), .b(32'h20000000), .gt(comparator_11_gt),
    .eq(comparator_11_eq));  // open: lt
  Comparator #(.width(32)) comparator_12 (
    .a({RGB_Address_Ensure, out_4, RAM_Byte_SEL}), .b(32'h20040000), .eq(comparator_12_eq),
    .lt(comparator_12_lt));  // open: gt
  and and_1 (and_1_out, not_2_out, or_5_out);
  and and_2 (and_2_out, not_2_out, or_6_out);
  Comparator #(.width(16)) comparator_13 (.a(adder_2_out), .b(16'h1770), .eq(STOP));  // open: gt, lt
  or or_7 (or_7_out, comparator_11_gt, comparator_11_eq);
  and and_3 (isRGB, or_7_out, or_8_out);
  or or_8 (or_8_out, comparator_12_eq, comparator_12_lt);
  Decoder #(.enable("false"), .select(2)) decoder_1 (
    .out0(decoder_1_out0), .out1(decoder_1_out1), .out2(decoder_1_out2), .out3(decoder_1_out3),
    .sel(RAM_Byte_SEL));
  RAM #(.addrWidth(24), .asyncread("true"), .byteenables("byteEnables"), .dataWidth(32), .\type ("nonvolatile")) ram_1 (
    .addr(out_4), .we(and_2_out), .oe(and_1_out), .clk(CLK), .din(out_5),
    .dout({Byte3, Byte2, Byte1, Byte0}), .be3(BE3), .be2(BE2), .be1(BE1), .be0(BE0));
  Comparator #(.width(3)) comparator_14 (.a(out_8), .b(3'b110), .eq(comparator_14_eq));  // open: gt, lt
  Comparator #(.width(3)) comparator_15 (.a(out_8), .b(3'b110), .eq(comparator_15_eq));  // open: gt, lt
  or or_9 (BE0, comparator_14_eq, decoder_1_out0);
  or or_10 (BE3, comparator_15_eq, decoder_1_out3);
  Comparator #(.width(3)) comparator_16 (.a(out_8), .b(3'b110), .eq(comparator_16_eq));  // open: gt, lt
  Comparator #(.width(3)) comparator_17 (.a(out_8), .b(3'b110), .eq(comparator_17_eq));  // open: gt, lt
  Multiplexer #(.select(2), .width(8)) multiplexer_4 (
    .in0(Byte0), .in1(Byte1), .in2(Byte2), .in3(Byte3), .out(LBU_Result), .sel(RAM_Byte_SEL));
  // RGB_Video #(.cursor("No Cursor"), .height(256), .scale(3), .width(256)) rgb_video_1: pin names not known; wires that end beside it: CLK, rgb_video_1_p2, out_4[7:0], out_4[15:8], rgb_video_1_p5
  and and_4 (rgb_video_1_p2, isRGB, comparator_16_eq);
  or or_11 (BE1, comparator_17_eq, decoder_1_out1);
  Comparator #(.width(3)) comparator_18 (.a(out_8), .b(3'b110), .eq(comparator_18_eq));  // open: gt, lt
  assign out_6 = {{20{Command[31]}}, {Command[31:25], Command[11:7]}};  // Bit_Extender bit_extender_2
  Multiplexer #(.width(24)) multiplexer_5 (.in1(out_7[23:0]), .out(rgb_video_1_p5), .sel(isRGB));  // open: in0
  or or_12 (BE2, comparator_18_eq, decoder_1_out2);

  assign out_3 = Command[24:20];
  assign out_11 = out_6;

  // Other names for the same wires on the sheet: rs2_data[31:0] = out_7; imm4_0[4:0] = Command[11:7];
  //   rd[4:0] = Command[11:7]; imm11_0[11:0] = Command[31:20]; imm11_5[6:0] = Command[31:25];
  //   LUI_Result[31:12] = Command[31:12]; CurrentPC[31:0] = PC; funct3[2:0] = Command[14:12];
  //   rs1[4:0] = Command[19:15]; rs2[4:0] = Command[24:20]; op[2:0] = out_8;
  //   RAM_Data_Out[31:0] = {Byte3, Byte2, Byte1, Byte0}; RGB_Address_Ensure[25:0] = {out_4, RAM_Byte_SEL};
  //   RAM_Address[23:0] = out_4; rs1_data[31:0] = out_10; Store_Data[31:0] = out_5; Store_imm[31:0] = out_6;
  //   Store_Result[31:0] = out_9

  // Notes on the sheet:
  //   contents of rom_1 (hex, n*v repeats v):
  //   413 93137 10113 10b7 dbc08093 80e7 fe012823 fea10923 fea12423 fe914203 fe4109a3 ff012783 f787b3
  //   f787b3 4b6b7 af868693 fdc10113 d787b3 10000713 f12423 10593 100793 b00513 2112023 12023 12223 e12623
  //   e12823 f10a23 10b7 a8408093 80e7 2012083 2410113 8067 ff410113 112423 10b7 a7c08093 80e7 513 1800093
  //   80e7 812083 513 c10113 8067 852583 feb12823 fe812e23 3437 80840413 ff014183 3401b3 1c183 ff114203
  //   440233 24203 4181b3 ff214203 440233 24203 4181b3 ff314203 440233 24203 4181b3 3237 80020213 320233
  //   24203 ffc12403 420233 420233 410233 11b7 86418193 fe312823 14800193 fe312623 fec22203 20067 1052703
  //   52683 452783 fe810113 e12423 112a23 812823 912623 fed12823 fef12623 13737 a0070713 fe012223 ff314203
  //   fe4102a3 fef14203 fe410223 fe412203 470233 24203 fe4105a3 ff214203 fe4102a3 fee14203 fe410223
  //   fe412203 470233 24203 fe410523 ff114203 fe4102a3 fed14203 fe410223 fe412203 470233 24203 fe4104a3
  //   ff014203 fe4102a3 fec14203 fe410223 fe412203 470233 24203 fe410423 fe812703 c52603 fee12823 fe812e23
  //   3437 80840413 ff014183 3401b3 1c183 ff114203 440233 24203 4181b3 ff214203 440233 24203 4181b3
  //   ff314203 440233 24203 4181b3 3237 80020213 320233 24203 ffc12403 420233 420233 410233 66800193
  //   fe312823 28800193 fe312623 fec22203 20067 c68733 10000513 fe812e23 fe912c23 fee12823 50413 ff012483
  //   fe812423 feb14183 3181b3 fe312423 fe914183 3181b3 fe912423 feb14203 420233 fe412423 fe914203 4181b3
  //   3181b3 fe312a23 fe912423 33237 90020213 feb14183 4181b3 1c183 fe3103a3 fea14183 4181b3 1c183
  //   fe310323 fe914183 4181b3 1c183 fe3102a3 fe814183 4181b3 1c183 fe310223 ff412183 fe412203 440233
  //   120213 fe412423 feb14203 420233 fe412423 fe914203 4181b3 3237 90820213 320233 ff812483 ffc12403
  //   24203 420233 420233 410233 11b7 86818193 fe312823 39000193 fe312623 fec22203 20067 812703 10000513
  //   e78733 fe812e23 fe912c23 fee12823 50413 ff012483 fe812423 feb14183 3181b3 fe312423 fe914183 3181b3
  //   fe912423 feb14203 420233 fe412423 fe914203 4181b3 3181b3 fe312a23 fe912423 33237 90020213 feb14183
  //   4181b3 1c183 fe3103a3 fea14183 4181b3 1c183 fe310323 fe914183 4181b3 1c183 fe3102a3 fe814183 4181b3
  //   1c183 fe310223 ff412183 fe412203 440233 120213 fe412423 feb14203 420233 fe412423 fe914203 4181b3
  //   3237 90820213 320233 ff812483 ffc12403 24203 420233 420233 410233 11b7 86818193 fe312823 49c00193
  //   fe312623 fec22203 20067 8*f787b3 d787b3 f787b3 f787b3 20000437 f40433 812783 c60633 c60633 fef12423
  //   feb14183 3181b3 fe312423 fe914183 fff78213 fe412423 feb14203 420233 fe412423 fe914203 4181b3 3237
  //   91820213 418233 24203 420233 420233 410233 65400193 fe312823 54000193 fe312623 fec22203 20067 493
  //   40513 b12223 c12023 10b7 de008093 80e7 12603 412583 812783 148493 40040413 c585b3 fef12823 fe912623
  //   fe812e23 fe912c23 2437 70040413 ff014183 340233 100193 320023 fec14183 3401b3 18023 24183 ff114483
  //   940233 100493 920023 fed14483 9404b3 48023 24483 9181b3 ff214483 940233 100493 920023 fee14483
  //   9404b3 48023 24483 9181b3 ff314483 940233 100493 920023 fef14483 9404b3 48023 24483 9181b3 3237
  //   80020213 320233 24203 ff812483 ffc12403 420233 420233 410233 65400193 fe312823 54400193 fe312623
  //   fec22203 20067 1412083 1012403 c12483 1810113 8067 10000713 fec12823 fee12623 fe812e23 fe912c23 2437
  //   70040413 ff014183 340233 100193 320023 fec14183 3401b3 18023 24183 ff114483 940233 100493 920023
  //   fed14483 9404b3 48023 24483 9181b3 ff214483 940233 100493 920023 fee14483 9404b3 48023 24483 9181b3
  //   ff314483 940233 100493 920023 fef14483 9404b3 48023 24483 9181b3 3237 80020213 320233 24203 ff812483
  //   ffc12403 420233 420233 410233 74c00193 fe312823 28800193 fe312623 fec22203 20067 812703 fee12823
  //   fec12623 fe812e23 fe912c23 2437 70040413 ff014183 340233 100193 320023 fec14183 3401b3 18023 24183
  //   ff114483 940233 100493 920023 fed14483 9404b3 48023 24483 9181b3 ff214483 940233 100493 920023
  //   fee14483 9404b3 48023 24483 9181b3 ff314483 940233 100493 920023 fef14483 9404b3 48023 24483 9181b3
  //   3237 80020213 320233 24203 ff812483 ffc12403 420233 420233 410233 11b7 83418193 fe312823 39000193
  //   fe312623 fec22203 20067 1012403 1412083 c12483 40637 20000537 1810113 1237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
endmodule

module GPR (
  input  [4:0] rs1_addr,
  input  clk,
  input  [31:0] wdata,
  input  reset,
  input  [4:0] rd_address,
  input  WE,
  input  [4:0] rs2_addr,
  output [31:0] rs1_val,
  output [31:0] rs2_val
);

  wire decoder_1_out1, decoder_1_out2, decoder_1_out3, decoder_1_out4, decoder_1_out5, decoder_1_out6,
       decoder_1_out7, decoder_1_out8, decoder_1_out9, decoder_1_out10, decoder_1_out11, decoder_1_out12,
       decoder_1_out13, decoder_1_out14, decoder_1_out15, decoder_2_out0, decoder_2_out1, decoder_2_out2,
       decoder_2_out3, decoder_2_out4, decoder_2_out5, decoder_2_out6, decoder_2_out7, decoder_2_out8,
       decoder_2_out9, decoder_2_out10, decoder_2_out11, decoder_2_out12, decoder_2_out13, decoder_2_out14,
       decoder_2_out15, not_1_out;
  wire [4:0] and_1_out, bit_extender_1_out;
  wire [31:0] a0_q, a1_q, a2_q, a3_q, a4_q, a5_q, a6_q, a7_q, gp_q, multiplexer_1_out, multiplexer_2_out,
       multiplexer_3_out, multiplexer_4_out, ra_q, s0_fp_q, s1_q, s2_q, s3_q, s4_q, s5_q, s6_q, s7_q, s8_q,
       s9_q, s10_q, s11_q, sp_q, t0_q, t1_q, t2_q, t3_q, t4_q, t5_q, t6_q, tp_q, ZERO_q;

  assign bit_extender_1_out = {{4{WE}}, WE};  // Bit_Extender bit_extender_1
  assign and_1_out = rd_address & bit_extender_1_out;  // AND_Gate and_1, 5 bits wide
  not not_1 (not_1_out, and_1_out[4]);
  Decoder #(.select(4)) decoder_1 (
    .out1(decoder_1_out1), .out2(decoder_1_out2), .out3(decoder_1_out3), .out4(decoder_1_out4),
    .out5(decoder_1_out5), .out6(decoder_1_out6), .out7(decoder_1_out7), .out8(decoder_1_out8),
    .out9(decoder_1_out9), .out10(decoder_1_out10), .out11(decoder_1_out11), .out12(decoder_1_out12),
    .out13(decoder_1_out13), .out14(decoder_1_out14), .out15(decoder_1_out15), .sel(and_1_out[3:0]),
    .en(not_1_out));  // open: out0
  Decoder #(.select(4)) decoder_2 (
    .out0(decoder_2_out0), .out1(decoder_2_out1), .out2(decoder_2_out2), .out3(decoder_2_out3),
    .out4(decoder_2_out4), .out5(decoder_2_out5), .out6(decoder_2_out6), .out7(decoder_2_out7),
    .out8(decoder_2_out8), .out9(decoder_2_out9), .out10(decoder_2_out10), .out11(decoder_2_out11),
    .out12(decoder_2_out12), .out13(decoder_2_out13), .out14(decoder_2_out14), .out15(decoder_2_out15),
    .sel(and_1_out[3:0]), .en(and_1_out[4]));
  Register #(.width(32)) ZERO (.D({32{1'b0}}), .en(1'b1), .clk(clk), .Q(ZERO_q), .clr(reset));
  Register #(.width(32)) s0_fp (.D(wdata), .en(decoder_1_out8), .clk(clk), .Q(s0_fp_q), .clr(reset));
  Register #(.width(32)) a6 (.D(wdata), .en(decoder_2_out0), .clk(clk), .Q(a6_q), .clr(reset));
  Register #(.width(32)) s8 (.D(wdata), .en(decoder_2_out8), .clk(clk), .Q(s8_q), .clr(reset));
  Register #(.width(32)) ra (.D(wdata), .en(decoder_1_out1), .clk(clk), .Q(ra_q), .clr(reset));
  Register #(.width(32)) s1 (.D(wdata), .en(decoder_1_out9), .clk(clk), .Q(s1_q), .clr(reset));
  Register #(.width(32)) a7 (.D(wdata), .en(decoder_2_out1), .clk(clk), .Q(a7_q), .clr(reset));
  Register #(.width(32)) s9 (.D(wdata), .en(decoder_2_out9), .clk(clk), .Q(s9_q), .clr(reset));
  Register #(.width(32)) sp (.D(wdata), .en(decoder_1_out2), .clk(clk), .Q(sp_q), .clr(reset));
  Register #(.width(32)) a0 (.D(wdata), .en(decoder_1_out10), .clk(clk), .Q(a0_q), .clr(reset));
  Register #(.width(32)) s2 (.D(wdata), .en(decoder_2_out2), .clk(clk), .Q(s2_q), .clr(reset));
  Register #(.width(32)) s10 (.D(wdata), .en(decoder_2_out10), .clk(clk), .Q(s10_q), .clr(reset));
  Register #(.width(32)) gp (.D(wdata), .en(decoder_1_out3), .clk(clk), .Q(gp_q), .clr(reset));
  Register #(.width(32)) a1 (.D(wdata), .en(decoder_1_out11), .clk(clk), .Q(a1_q), .clr(reset));
  Register #(.width(32)) s3 (.D(wdata), .en(decoder_2_out3), .clk(clk), .Q(s3_q), .clr(reset));
  Register #(.width(32)) s11 (.D(wdata), .en(decoder_2_out11), .clk(clk), .Q(s11_q), .clr(reset));
  Register #(.width(32)) tp (.D(wdata), .en(decoder_1_out4), .clk(clk), .Q(tp_q), .clr(reset));
  Register #(.width(32)) a2 (.D(wdata), .en(decoder_1_out12), .clk(clk), .Q(a2_q), .clr(reset));
  Register #(.width(32)) s4 (.D(wdata), .en(decoder_2_out4), .clk(clk), .Q(s4_q), .clr(reset));
  Register #(.width(32)) t3 (.D(wdata), .en(decoder_2_out12), .clk(clk), .Q(t3_q), .clr(reset));
  Register #(.width(32)) t0 (.D(wdata), .en(decoder_1_out5), .clk(clk), .Q(t0_q), .clr(reset));
  Register #(.width(32)) a3 (.D(wdata), .en(decoder_1_out13), .clk(clk), .Q(a3_q), .clr(reset));
  Register #(.width(32)) s5 (.D(wdata), .en(decoder_2_out5), .clk(clk), .Q(s5_q), .clr(reset));
  Register #(.width(32)) t4 (.D(wdata), .en(decoder_2_out13), .clk(clk), .Q(t4_q), .clr(reset));
  Register #(.width(32)) t1 (.D(wdata), .en(decoder_1_out6), .clk(clk), .Q(t1_q), .clr(reset));
  Register #(.width(32)) a4 (.D(wdata), .en(decoder_1_out14), .clk(clk), .Q(a4_q), .clr(reset));
  Register #(.width(32)) s6 (.D(wdata), .en(decoder_2_out6), .clk(clk), .Q(s6_q), .clr(reset));
  Register #(.width(32)) t5 (.D(wdata), .en(decoder_2_out14), .clk(clk), .Q(t5_q), .clr(reset));
  Register #(.width(32)) t2 (.D(wdata), .en(decoder_1_out7), .clk(clk), .Q(t2_q), .clr(reset));
  Register #(.width(32)) a5 (.D(wdata), .en(decoder_1_out15), .clk(clk), .Q(a5_q), .clr(reset));
  Register #(.width(32)) s7 (.D(wdata), .en(decoder_2_out7), .clk(clk), .Q(s7_q), .clr(reset));
  Register #(.width(32)) t6 (.D(wdata), .en(decoder_2_out15), .clk(clk), .Q(t6_q), .clr(reset));
  Multiplexer #(.select(4), .width(32)) multiplexer_1 (
    .in0(ZERO_q), .in1(ra_q), .in2(sp_q), .in3(gp_q), .in4(tp_q), .in5(t0_q), .in6(t1_q), .in7(t2_q),
    .in8(s0_fp_q), .in9(s1_q), .in10(a0_q), .in11(a1_q), .in12(a2_q), .in13(a3_q), .in14(a4_q), .in15(a5_q),
    .out(multiplexer_1_out), .sel(rs1_addr[3:0]));
  Multiplexer #(.select(4), .width(32)) multiplexer_2 (
    .in0(ZERO_q), .in1(ra_q), .in2(sp_q), .in3(gp_q), .in4(tp_q), .in5(t0_q), .in6(t1_q), .in7(t2_q),
    .in8(s0_fp_q), .in9(s1_q), .in10(a0_q), .in11(a1_q), .in12(a2_q), .in13(a3_q), .in14(a4_q), .in15(a5_q),
    .out(multiplexer_2_out), .sel(rs2_addr[3:0]));
  Multiplexer #(.select(4), .width(32)) multiplexer_3 (
    .in0(a6_q), .in1(a7_q), .in2(s2_q), .in3(s3_q), .in4(s4_q), .in5(s5_q), .in6(s6_q), .in7(s7_q),
    .in8(s8_q), .in9(s9_q), .in10(s10_q), .in11(s11_q), .in12(t3_q), .in13(t4_q), .in14(t5_q), .in15(t6_q),
    .out(multiplexer_3_out), .sel(rs1_addr[3:0]));
  Multiplexer #(.select(4), .width(32)) multiplexer_4 (
    .in0(a6_q), .in1(a7_q), .in2(s2_q), .in3(s3_q), .in4(s4_q), .in5(s5_q), .in6(s6_q), .in7(s7_q),
    .in8(s8_q), .in9(s9_q), .in10(s10_q), .in11(s11_q), .in12(t3_q), .in13(t4_q), .in14(t5_q), .in15(t6_q),
    .out(multiplexer_4_out), .sel(rs2_addr[3:0]));
  Multiplexer #(.width(32)) multiplexer_5 (
    .in0(multiplexer_1_out), .in1(multiplexer_3_out), .out(rs1_val), .sel(rs1_addr[4]));
  Multiplexer #(.width(32)) multiplexer_6 (
    .in0(multiplexer_2_out), .in1(multiplexer_4_out), .out(rs2_val), .sel(rs2_addr[4]));
endmodule

module ProgramCounter (
  input  [2:0] Op,
  input  [31:0] PC_input,
  input  clk,
  output [31:0] CurrentPC,
  output [31:0] NextPC
);

  wire [31:0] adder_1_out;

  Adder #(.width(32)) adder_1 (.a(32'h4), .b(CurrentPC), .out(adder_1_out));  // open: cin, cout
  Multiplexer #(.select(3), .width(32)) multiplexer_1 (
    .in0(adder_1_out), .in1({PC_input[31:1], 1'b0}), .in2(adder_1_out), .in3(adder_1_out), .in4(adder_1_out),
    .in5(adder_1_out), .in6(adder_1_out), .in7(adder_1_out), .out(NextPC), .sel(Op));
  Register #(.width(32)) register_1 (.D(NextPC), .en(1'b1), .clk(clk), .Q(CurrentPC), .clr(1'b0));
endmodule

module OpCoder (
  input  [6:0] funct7,
  input  [6:0] OpCode,
  input  [2:0] funct3,
  output [2:0] op
);

  wire and_1_out, and_2_out, and_3_out, and_4_out, and_5_out, comparator_1_eq, comparator_2_eq,
       comparator_3_eq, comparator_4_eq, comparator_5_eq, comparator_6_eq, comparator_7_eq, comparator_8_eq,
       comparator_9_eq, comparator_10_eq, comparator_11_eq, comparator_12_eq, comparator_13_eq;

  Comparator #(.width(7)) comparator_1 (.a(funct7), .b({7{1'b0}}), .eq(comparator_1_eq));  // open: gt, lt
  Comparator #(.width(7)) comparator_2 (.a(OpCode), .b(7'b0010011), .eq(comparator_2_eq));  // open: gt, lt
  Comparator #(.width(7)) comparator_3 (.a(OpCode), .b(7'b1100111), .eq(comparator_3_eq));  // open: gt, lt
  Comparator #(.width(7)) comparator_4 (.a(OpCode), .b(7'b0110011), .eq(comparator_4_eq));  // open: gt, lt
  Comparator #(.width(7)) comparator_5 (.a(OpCode), .b(7'b0110111), .eq(comparator_5_eq));  // open: gt, lt
  Comparator #(.width(7)) comparator_6 (.a(OpCode), .b(7'b0000011), .eq(comparator_6_eq));  // open: gt, lt
  Comparator #(.width(3)) comparator_7 (.a(funct3), .b(3'b010), .eq(comparator_7_eq));  // open: gt, lt
  Comparator #(.width(7)) comparator_8 (.a(OpCode), .b(7'b0000011), .eq(comparator_8_eq));  // open: gt, lt
  Comparator #(.width(3)) comparator_9 (.a(funct3), .b(3'b100), .eq(comparator_9_eq));  // open: gt, lt
  Comparator #(.width(7)) comparator_10 (.a(OpCode), .b(7'b0100011), .eq(comparator_10_eq));  // open: gt, lt
  Comparator #(.width(3)) comparator_11 (.a(funct3), .b(3'b010), .eq(comparator_11_eq));  // open: gt, lt
  Comparator #(.width(7)) comparator_12 (.a(OpCode), .b(7'b0100011), .eq(comparator_12_eq));  // open: gt, lt
  Comparator #(.width(3)) comparator_13 (.a(funct3), .b(3'b000), .eq(comparator_13_eq));  // open: gt, lt
  and and_1 (and_1_out, comparator_1_eq, comparator_4_eq);
  and and_2 (and_2_out, comparator_6_eq, comparator_7_eq);
  and and_3 (and_3_out, comparator_8_eq, comparator_9_eq);
  and and_4 (and_4_out, comparator_10_eq, comparator_11_eq);
  and and_5 (and_5_out, comparator_12_eq, comparator_13_eq);
  Priority_Encoder priority_encoder_1 (
    .in0(comparator_2_eq), .in1(comparator_3_eq), .in2(and_1_out), .in3(comparator_5_eq), .in4(and_2_out),
    .in5(and_3_out), .in6(and_4_out), .in7(and_5_out), .out(op), .en_in(1'b1));  // open: gs, en_out
endmodule

module ALU (
  input  [31:0] A,
  input  [31:0] B,
  output [31:0] Sum
);

  wire [31:0] adder_1_out, adder_2_out, adder_3_out, adder_4_out, adder_5_out, not_1_out, not_2_out,
       not_3_out, subtractor_1_out, subtractor_2_out;

  assign not_1_out = ~A;  // NOT_Gate not_1, 32 bits wide
  Adder #(.width(32)) adder_1 (.a(not_1_out), .b(32'h1), .out(adder_1_out));  // open: cin, cout
  assign not_2_out = ~B;  // NOT_Gate not_2, 32 bits wide
  Adder #(.width(32)) adder_2 (.a(not_2_out), .b(32'h1), .out(adder_2_out));  // open: cin, cout
  Adder #(.width(32)) adder_3 (.a(A), .b(B), .out(adder_3_out));  // open: cin, cout
  Subtractor #(.width(32)) subtractor_1 (.a(B), .b(adder_1_out), .out(subtractor_1_out));  // open: bin, bout
  Subtractor #(.width(32)) subtractor_2 (.a(A), .b(adder_2_out), .out(subtractor_2_out));  // open: bin, bout
  Adder #(.width(32)) adder_4 (.a(adder_1_out), .b(adder_2_out), .out(adder_4_out));  // open: cin, cout
  assign not_3_out = ~adder_4_out;  // NOT_Gate not_3, 32 bits wide
  Adder #(.width(32)) adder_5 (.a(not_3_out), .b(32'h1), .out(adder_5_out));  // open: cin, cout
  Multiplexer #(.select(2), .width(32)) multiplexer_1 (
    .in0(adder_3_out), .in1(subtractor_1_out), .in2(subtractor_2_out), .in3(adder_5_out), .out(Sum),
    .sel({B[31], A[31]}));
endmodule
