// Logisim project F6Fail.circ as structural Verilog
module ProgramCounter (
  input  [31:0] NEXT_PC,
  input  CLK,
  input  RESET_PC,
  output [31:0] CURRENT_PC
);

  Register #(.width(32)) register_1 (.D(NEXT_PC), .en(1'b1), .clk(CLK), .Q(CURRENT_PC), .clr(RESET_PC));
endmodule

module GPR (
  input  clk,
  input  [31:0] wdata,
  input  [4:0] ADDR,
  input  WE,
  input  [4:0] READ1,
  input  [4:0] READ2,
  output [31:0] Q,
  output [31:0] OUT1,
  output [31:0] OUT2
);

  wire and_1_out, and_2_out, decoder_1_out1, decoder_1_out2, decoder_1_out3, decoder_1_out4, decoder_1_out5,
       decoder_1_out6, decoder_1_out7, decoder_1_out8, decoder_1_out9, decoder_1_out10, decoder_1_out11,
       decoder_1_out12, decoder_1_out13, decoder_1_out14, decoder_1_out15, decoder_2_out0, decoder_2_out1,
       decoder_2_out2, decoder_2_out3, decoder_2_out4, decoder_2_out5, decoder_2_out6, decoder_2_out7,
       decoder_2_out8, decoder_2_out9, decoder_2_out10, decoder_2_out11, decoder_2_out12, decoder_2_out13,
       decoder_2_out14, decoder_2_out15, not_1_out, not_2_out, not_3_out, not_4_out;
  wire [31:0] multiplexer_1_out, multiplexer_2_out, multiplexer_3_out, multiplexer_4_out, multiplexer_5_out,
       multiplexer_6_out, R00_q, R0a_q, R0b_q, R0c_q, R0d_q, R0e_q, R0f_q, R01_q, R1a_q, R1b_q, R1c_q, R1d_q,
       R1e_q, R1f_q, R02_q, R03_q, R04_q, R05_q, R06_q, R07_q, R08_q, R09_q, R10_q, R11_q, R12_q, R13_q,
       R14_q, R15_q, R16_q, R17_q, R18_q, R19_q;

  not not_1 (not_1_out, ADDR[4]);
  and and_1 (and_1_out, not_1_out, WE);
  and and_2 (and_2_out, ADDR[4], WE);
  Decoder #(.select(4)) decoder_1 (
    .out1(decoder_1_out1), .out2(decoder_1_out2), .out3(decoder_1_out3), .out4(decoder_1_out4),
    .out5(decoder_1_out5), .out6(decoder_1_out6), .out7(decoder_1_out7), .out8(decoder_1_out8),
    .out9(decoder_1_out9), .out10(decoder_1_out10), .out11(decoder_1_out11), .out12(decoder_1_out12),
    .out13(decoder_1_out13), .out14(decoder_1_out14), .out15(decoder_1_out15), .sel(ADDR[3:0]), .en(and_1_out));  // open: out0
  Decoder #(.select(4)) decoder_2 (
    .out0(decoder_2_out0), .out1(decoder_2_out1), .out2(decoder_2_out2), .out3(decoder_2_out3),
    .out4(decoder_2_out4), .out5(decoder_2_out5), .out6(decoder_2_out6), .out7(decoder_2_out7),
    .out8(decoder_2_out8), .out9(decoder_2_out9), .out10(decoder_2_out10), .out11(decoder_2_out11),
    .out12(decoder_2_out12), .out13(decoder_2_out13), .out14(decoder_2_out14), .out15(decoder_2_out15),
    .sel(ADDR[3:0]), .en(and_2_out));
  Register #(.width(32)) R00 (.D({32{1'b0}}), .en(1'b0), .clk(clk), .Q(R00_q));  // open: clr
  Register #(.width(32)) R08 (.D(wdata), .en(decoder_1_out8), .clk(clk), .Q(R08_q));  // open: clr
  Register #(.width(32)) R10 (.D(wdata), .en(decoder_2_out0), .clk(clk), .Q(R10_q));  // open: clr
  Register #(.width(32)) R18 (.D(wdata), .en(decoder_2_out8), .clk(clk), .Q(R18_q));  // open: clr
  Register #(.width(32)) R01 (.D(wdata), .en(decoder_1_out1), .clk(clk), .Q(R01_q));  // open: clr
  Register #(.width(32)) R09 (.D(wdata), .en(decoder_1_out9), .clk(clk), .Q(R09_q));  // open: clr
  Register #(.width(32)) R11 (.D(wdata), .en(decoder_2_out1), .clk(clk), .Q(R11_q));  // open: clr
  Register #(.width(32)) R19 (.D(wdata), .en(decoder_2_out9), .clk(clk), .Q(R19_q));  // open: clr
  Register #(.width(32)) R02 (.D(wdata), .en(decoder_1_out2), .clk(clk), .Q(R02_q));  // open: clr
  Register #(.width(32)) R0a (.D(wdata), .en(decoder_1_out10), .clk(clk), .Q(R0a_q));  // open: clr
  Register #(.width(32)) R12 (.D(wdata), .en(decoder_2_out2), .clk(clk), .Q(R12_q));  // open: clr
  Register #(.width(32)) R1a (.D(wdata), .en(decoder_2_out10), .clk(clk), .Q(R1a_q));  // open: clr
  Register #(.width(32)) R03 (.D(wdata), .en(decoder_1_out3), .clk(clk), .Q(R03_q));  // open: clr
  Register #(.width(32)) R0b (.D(wdata), .en(decoder_1_out11), .clk(clk), .Q(R0b_q));  // open: clr
  Register #(.width(32)) R13 (.D(wdata), .en(decoder_2_out3), .clk(clk), .Q(R13_q));  // open: clr
  Register #(.width(32)) R1b (.D(wdata), .en(decoder_2_out11), .clk(clk), .Q(R1b_q));  // open: clr
  Register #(.width(32)) R04 (.D(wdata), .en(decoder_1_out4), .clk(clk), .Q(R04_q));  // open: clr
  Register #(.width(32)) R0c (.D(wdata), .en(decoder_1_out12), .clk(clk), .Q(R0c_q));  // open: clr
  Register #(.width(32)) R14 (.D(wdata), .en(decoder_2_out4), .clk(clk), .Q(R14_q));  // open: clr
  Register #(.width(32)) R1c (.D(wdata), .en(decoder_2_out12), .clk(clk), .Q(R1c_q));  // open: clr
  Register #(.width(32)) R05 (.D(wdata), .en(decoder_1_out5), .clk(clk), .Q(R05_q));  // open: clr
  Register #(.width(32)) R0d (.D(wdata), .en(decoder_1_out13), .clk(clk), .Q(R0d_q));  // open: clr
  Register #(.width(32)) R15 (.D(wdata), .en(decoder_2_out5), .clk(clk), .Q(R15_q));  // open: clr
  Register #(.width(32)) R1d (.D(wdata), .en(decoder_2_out13), .clk(clk), .Q(R1d_q));  // open: clr
  Register #(.width(32)) R06 (.D(wdata), .en(decoder_1_out6), .clk(clk), .Q(R06_q));  // open: clr
  Register #(.width(32)) R0e (.D(wdata), .en(decoder_1_out14), .clk(clk), .Q(R0e_q));  // open: clr
  Register #(.width(32)) R16 (.D(wdata), .en(decoder_2_out6), .clk(clk), .Q(R16_q));  // open: clr
  Register #(.width(32)) R1e (.D(wdata), .en(decoder_2_out14), .clk(clk), .Q(R1e_q));  // open: clr
  Register #(.width(32)) R07 (.D(wdata), .en(decoder_1_out7), .clk(clk), .Q(R07_q));  // open: clr
  Register #(.width(32)) R0f (.D(wdata), .en(decoder_1_out15), .clk(clk), .Q(R0f_q));  // open: clr
  Register #(.width(32)) R17 (.D(wdata), .en(decoder_2_out7), .clk(clk), .Q(R17_q));  // open: clr
  Register #(.width(32)) R1f (.D(wdata), .en(decoder_2_out15), .clk(clk), .Q(R1f_q));  // open: clr
  not not_2 (not_2_out, READ1[4]);
  Multiplexer #(.enable("true"), .select(4), .width(32)) multiplexer_1 (
    .in0(R00_q), .in1(R01_q), .in2(R02_q), .in3(R03_q), .in4(R04_q), .in5(R05_q), .in6(R06_q), .in7(R07_q),
    .in8(R08_q), .in9(R09_q), .in10(R0a_q), .in11(R0b_q), .in12(R0c_q), .in13(R0d_q), .in14(R0e_q),
    .in15(R0f_q), .out(multiplexer_1_out), .sel(READ2[3:0]), .en(not_4_out));
  not not_3 (not_3_out, ADDR[4]);
  Multiplexer #(.enable("true"), .select(4), .width(32)) multiplexer_2 (
    .in0(R00_q), .in1(R01_q), .in2(R02_q), .in3(R03_q), .in4(R04_q), .in5(R05_q), .in6(R06_q), .in7(R07_q),
    .in8(R08_q), .in9(R09_q), .in10(R0a_q), .in11(R0b_q), .in12(R0c_q), .in13(R0d_q), .in14(R0e_q),
    .in15(R0f_q), .out(multiplexer_2_out), .sel(ADDR[3:0]), .en(not_3_out));
  Multiplexer #(.enable("true"), .select(4), .width(32)) multiplexer_3 (
    .in0(R00_q), .in1(R01_q), .in2(R02_q), .in3(R03_q), .in4(R04_q), .in5(R05_q), .in6(R06_q), .in7(R07_q),
    .in8(R08_q), .in9(R09_q), .in10(R0a_q), .in11(R0b_q), .in12(R0c_q), .in13(R0d_q), .in14(R0e_q),
    .in15(R0f_q), .out(multiplexer_3_out), .sel(READ1[3:0]), .en(not_2_out));
  Multiplexer #(.enable("true"), .select(4), .width(32)) multiplexer_4 (
    .in0(R10_q), .in1(R11_q), .in2(R12_q), .in3(R13_q), .in4(R14_q), .in5(R15_q), .in6(R16_q), .in7(R17_q),
    .in8(R18_q), .in9(R19_q), .in10(R1a_q), .in11(R1b_q), .in12(R1c_q), .in13(R1d_q), .in14(R1e_q),
    .in15(R1f_q), .out(multiplexer_4_out), .sel(ADDR[3:0]), .en(ADDR[4]));
  Multiplexer #(.enable("true"), .select(4), .width(32)) multiplexer_5 (
    .in0(R10_q), .in1(R11_q), .in2(R12_q), .in3(R13_q), .in4(R14_q), .in5(R15_q), .in6(R16_q), .in7(R17_q),
    .in8(R18_q), .in9(R19_q), .in10(R1a_q), .in11(R1b_q), .in12(R1c_q), .in13(R1d_q), .in14(R1e_q),
    .in15(R1f_q), .out(multiplexer_5_out), .sel(READ1[3:0]), .en(READ1[4]));
  Multiplexer #(.enable("true"), .select(4), .width(32)) multiplexer_6 (
    .in0(R10_q), .in1(R11_q), .in2(R12_q), .in3(R13_q), .in4(R14_q), .in5(R15_q), .in6(R16_q), .in7(R17_q),
    .in8(R18_q), .in9(R19_q), .in10(R1a_q), .in11(R1b_q), .in12(R1c_q), .in13(R1d_q), .in14(R1e_q),
    .in15(R1f_q), .out(multiplexer_6_out), .sel(READ2[3:0]), .en(READ2[4]));
  assign Q = multiplexer_2_out | multiplexer_4_out;  // OR_Gate or_1, 32 bits wide
  assign OUT1 = multiplexer_3_out | multiplexer_5_out;  // OR_Gate or_2, 32 bits wide
  not not_4 (not_4_out, READ2[4]);
  assign OUT2 = multiplexer_1_out | multiplexer_6_out;  // OR_Gate or_3, 32 bits wide
endmodule

module minirv (
  output [4:0] out_1,
  output [31:0] out_2,
  output [11:0] out_3,
  output [2:0] out_4,
  output [31:0] out_5,
  output [31:0] out_6,
  output [31:0] out_7,
  output [19:0] out_8,
  output [31:0] out_9,
  output [23:0] out_10,
  output [31:0] out_11,
  output [4:0] out_12
);

  wire and_11_out, and_12_out, and_13_out, and_14_out, CLK, comparator_3_eq, comparator_4_eq,
       comparator_13_eq, comparator_14_eq, comparator_15_eq, comparator_16_eq, comparator_17_eq,
       decoder_1_out0, decoder_1_out1, decoder_1_out2, decoder_1_out3, GPR_WE, not_1_out, not_2_out,
       or_1_out, Over6000, RAM_BE0, RAM_BE1, RAM_BE2, RAM_BE3, RAM_WE;
  wire [7:0] RAM_ReadOut_Byte;
  wire [23:0] and_3_out, and_4_out, and_5_out, and_6_out, RAM_Address;
  wire [23:23] comparator_5_eq, comparator_6_eq, comparator_7_eq, comparator_8_eq;
  wire [31:0] ALU_Result, and_1_out, and_2_out, and_7_out, and_8_out, and_9_out, and_10_out,
       bit_extender_1_out, ImmediateNumber32Bit, multiplexer_2_out, or_2_out, Plus4, RegisterData1,
       RegisterData2, RegisterDataDestination, WriteData;
  wire [31:31] comparator_1_eq, comparator_2_eq, comparator_9_eq, comparator_10_eq, comparator_11_eq,
       comparator_12_eq;
  wire [63:0] adder_2_out, register_1_q;

  not not_1 (not_1_out, Over6000);
  Clock clock_1 (.out(CLK));
  Comparator #(.width(3)) comparator_1 (.a(out_4), .b(3'b100), .eq(comparator_1_eq[31]));  // open: gt, lt
  Comparator #(.width(3)) comparator_2 (.a(out_4), .b(3'b101), .eq(comparator_2_eq[31]));  // open: gt, lt
  Comparator #(.width(3)) comparator_3 (.a(out_4), .b(3'b100), .eq(comparator_3_eq));  // open: gt, lt
  Comparator #(.width(3)) comparator_4 (.a(out_4), .b(3'b101), .eq(comparator_4_eq));  // open: gt, lt
  Comparator #(.width(3)) comparator_5 (.a(out_4), .b(3'b100), .eq(comparator_5_eq[23]));  // open: gt, lt
  Comparator #(.width(3)) comparator_6 (.a(out_4), .b(3'b101), .eq(comparator_6_eq[23]));  // open: gt, lt
  Comparator #(.width(3)) comparator_7 (.a(out_4), .b(3'b110), .eq(comparator_7_eq[23]));  // open: gt, lt
  Comparator #(.width(3)) comparator_8 (.a(out_4), .b(3'b111), .eq(comparator_8_eq[23]));  // open: gt, lt
  Multiplexer #(.select(3), .width(32)) multiplexer_1 (
    .in0(Plus4), .in1({ALU_Result[31:2], 2'b00}), .in2(Plus4), .in3(Plus4), .in4(Plus4), .in5(Plus4),
    .in6(Plus4), .in7(Plus4), .out(out_5), .sel(out_4));
  assign and_1_out = {32{comparator_1_eq[31]}} & out_11;  // AND_Gate and_1, 32 bits wide
  assign and_2_out = {32{comparator_2_eq[31]}} & {{24{1'b0}}, RAM_ReadOut_Byte};  // AND_Gate and_2, 32 bits wide
  Adder #(.width(32)) adder_1 (.a(out_6), .b(32'h4), .out(Plus4));  // open: cin, cout
  or or_1 (or_1_out, comparator_3_eq, comparator_4_eq);
  assign and_3_out = ALU_Result[25:2] & {24{comparator_5_eq[23]}};  // AND_Gate and_3, 24 bits wide
  assign and_4_out = ALU_Result[25:2] & {24{comparator_6_eq[23]}};  // AND_Gate and_4, 24 bits wide
  assign and_5_out = out_9[25:2] & {24{comparator_7_eq[23]}};  // AND_Gate and_5, 24 bits wide
  assign and_6_out = out_9[25:2] & {24{comparator_8_eq[23]}};  // AND_Gate and_6, 24 bits wide
  Multiplexer #(.select(3), .width(32)) multiplexer_2 (
    .in0(ImmediateNumber32Bit), .in1(ImmediateNumber32Bit), .in2(RegisterData2), .in3(ImmediateNumber32Bit),
    .in4(ImmediateNumber32Bit), .in5(ImmediateNumber32Bit), .in6(ImmediateNumber32Bit),
    .in7(ImmediateNumber32Bit), .out(multiplexer_2_out), .sel(out_4));
  Comparator #(.width(7)) comparator_9 (.a(out_2[6:0]), .b(7'b0110111), .eq(comparator_9_eq[31]));  // open: gt, lt
  Comparator #(.width(7)) comparator_10 (.a(out_2[6:0]), .b(7'b0110011), .eq(comparator_10_eq[31]));  // open: gt, lt
  Comparator #(.width(7)) comparator_11 (.a(out_2[6:0]), .b(7'b0010011), .eq(comparator_11_eq[31]));  // open: gt, lt
  Comparator #(.width(7)) comparator_12 (.a(out_2[6:0]), .b(7'b1100111), .eq(comparator_12_eq[31]));  // open: gt, lt
  Comparator #(.width(7)) comparator_13 (.a(out_2[6:0]), .b(7'b0000011), .eq(comparator_13_eq));  // open: gt, lt
  assign or_2_out = and_1_out | and_2_out;  // OR_Gate or_2, 32 bits wide
  assign RAM_Address = and_3_out | and_4_out | and_5_out | and_6_out;  // OR_Gate or_3, 24 bits wide
  ProgramCounter programcounter_1 (.NEXT_PC(out_5), .CLK(CLK), .CURRENT_PC(out_6));  // open: RESET_PC
  assign and_7_out = {32{comparator_11_eq[31]}} & ALU_Result;  // AND_Gate and_7, 32 bits wide
  assign and_8_out = {32{comparator_12_eq[31]}} & Plus4;  // AND_Gate and_8, 32 bits wide
  assign and_9_out = {32{comparator_10_eq[31]}} & ALU_Result;  // AND_Gate and_9, 32 bits wide
  assign and_10_out = {32{comparator_9_eq[31]}} & out_7;  // AND_Gate and_10, 32 bits wide
  not not_2 (not_2_out, CLK);
  or or_4 (GPR_WE, comparator_9_eq[31], comparator_10_eq[31], comparator_11_eq[31], comparator_12_eq[31], comparator_13_eq);
  assign WriteData = and_7_out | and_8_out | and_9_out | and_10_out | or_2_out;  // OR_Gate or_5, 32 bits wide
  ROM #(.addrWidth(24), .dataWidth(32)) IMEM (.addr(out_6[25:2]), .data({out_2[31:12], out_1, out_2[6:0]}));
  RAM #(.addrWidth(24), .asyncread("true"), .byteenables("byteEnables"), .dataWidth(32), .\type ("nonvolatile")) ram_1 (
    .addr(RAM_Address), .we(RAM_WE), .oe(or_1_out), .clk(not_2_out), .din(RegisterData2), .dout(out_11),
    .be3(RAM_BE3), .be2(RAM_BE2), .be1(RAM_BE1), .be0(RAM_BE0));
  GPR gpr_1 (
    .clk(CLK), .wdata(WriteData), .ADDR(out_1), .WE(GPR_WE), .READ1(out_2[19:15]), .READ2(out_2[24:20]),
    .Q(RegisterDataDestination), .OUT1(RegisterData1), .OUT2(RegisterData2));
  Extender12_32 extender12_32_1 (.SEL(out_2[6:0]), .Input12Bit(out_2[31:20]), .Output32Bit(ImmediateNumber32Bit));
  ALU alu_1 (
    .ImmediateNumber32Bit(multiplexer_2_out), .RegisterData1(RegisterData1), .SEL(out_2[6:0]),
    .Function3(out_2[14:12]), .S(ALU_Result), .OperationCode(out_4));
  Register #(.width(64)) register_1 (.D(adder_2_out), .en(1'b1), .clk(CLK), .Q(register_1_q));  // open: clr
  Extender20_32 extender20_32_1 (.Input20Bit(out_2[31:12]), .Output32Bit(out_7));
  assign bit_extender_1_out = {{20{out_2[31]}}, {out_2[31:25], out_1}};  // Bit_Extender bit_extender_1
  Comparator #(.width(3)) comparator_14 (.a(out_4), .b(3'b110), .eq(comparator_14_eq));  // open: gt, lt
  Decoder #(.enable("false"), .select(2)) decoder_1 (
    .out0(decoder_1_out0), .out1(decoder_1_out1), .out2(decoder_1_out2), .out3(decoder_1_out3),
    .sel(out_9[1:0]));
  Comparator #(.width(3)) comparator_15 (.a(out_4), .b(3'b111), .eq(comparator_15_eq));  // open: gt, lt
  Comparator #(.width(3)) comparator_16 (.a(out_4), .b(3'b110), .eq(comparator_16_eq));  // open: gt, lt
  Comparator #(.width(3)) comparator_17 (.a(out_4), .b(3'b111), .eq(comparator_17_eq));  // open: gt, lt
  or or_6 (RAM_WE, comparator_16_eq, comparator_17_eq);
  Adder #(.width(64)) adder_2 (.a(register_1_q), .b(64'h1), .out(adder_2_out));  // open: cin, cout
  and and_11 (and_11_out, decoder_1_out0, comparator_15_eq);
  and and_12 (and_12_out, decoder_1_out1, comparator_15_eq);
  and and_13 (and_13_out, decoder_1_out2, comparator_15_eq);
  and and_14 (and_14_out, decoder_1_out3, comparator_15_eq);
  Comparator #(.width(64)) comparator_18 (.a(adder_2_out), .b(64'h1772), .gt(Over6000));  // open: eq, lt
  Multiplexer #(.select(2), .width(8)) multiplexer_3 (
    .in0(out_11[7:0]), .in1(out_11[15:8]), .in2(out_11[23:16]), .in3(out_11[31:24]), .out(RAM_ReadOut_Byte),
    .sel(ALU_Result[1:0]));
  or or_7 (RAM_BE0, comparator_14_eq, and_11_out);
  or or_8 (RAM_BE1, comparator_14_eq, and_12_out);
  or or_9 (RAM_BE2, comparator_14_eq, and_13_out);
  or or_10 (RAM_BE3, comparator_14_eq, and_14_out);
  SignAdder signadder_1 (.ImmediateNumber32Bit(bit_extender_1_out), .RegisterData1(RegisterData1), .S(out_9));

  assign out_2[11:7] = out_1;
  assign out_3 = out_2[31:20];
  assign out_8 = out_2[31:12];
  assign out_10 = out_9[25:2];
  assign out_12 = out_1;

  // Other names for the same wires on the sheet: RegisterDestination[4:0] = out_1;
  //   ImmediateNumber12Bit[11:0] = out_2[31:20]; ImmediateNumber_1[6:0] = out_2[31:25];
  //   ByteSEL[1:0] = ALU_Result[1:0]; Current_PC[31:0] = out_6; JALRPC[31:2] = ALU_Result[31:2];
  //   WordSEL[23:0] = ALU_Result[25:2]; LUI_Number[31:0] = out_7; OperationCode[2:0] = out_4;
  //   OperationNumber[6:0] = out_2[6:0]; Function3[2:0] = out_2[14:12]; RegisterSource1[4:0] = out_2[19:15];
  //   RegisterSource2[4:0] = out_2[24:20]; RAM_Destination[31:0] = out_9; RAM_WriteByteSEL[1:0] = out_9[1:0];
  //   ImmediateNumberAddress[23:0] = out_9[25:2]; RAM_ReadOut[31:0] = out_11; RAM_ReadOut_8[7:0] = out_11[7:0];
  //   RAM_ReadOut_16[7:0] = out_11[15:8]; RAM_ReadOut_24[7:0] = out_11[23:16]; RAM_ReadOut_32[7:0] = out_11[31:24]

  // Notes on the sheet:
  //   contents of IMEM (hex, n*v repeats v):
  //   413 52137 10113 10b7 22408093 80e7 fea12823 fe812e23 1437 40840413 ff014183 3401b3 1c183 ff114203
  //   440233 24203 4181b3 ff214203 440233 24203 4181b3 ff314203 440233 24203 4181b3 1237 40020213 320233
  //   24203 ffc12403 420233 420233 410233 a000193 fe312823 9c00193 fe312623 fec22203 20067 8067 ff410113
  //   100513 112423 10b7 21808093 80e7 fec10113 912423 494b7 6b048493 812623 112823 496b7 69068693 48413
  //   48713 fe012823 174183 fe3109a3 ff012183 fe812e23 fe312823 3d437 60040413 ff214203 420233 420233
  //   440233 22203 fe412623 ff114203 420233 420233 440233 22203 fe412423 ff014203 420233 420233 440233
  //   22203 fe412223 fed14183 fea14203 4181b3 fe714203 4181b3 fe312223 fee14183 feb14203 4181b3 fe3102a3
  //   fef14183 fe310323 fe412183 8237 20213 440433 ff314203 420233 420233 440233 22203 ffc12403 4181b3
  //   74503 350533 6a603 270713 468693 fe312a23 fec12423 31237 50020213 feb14183 4181b3 1c183 fe3103a3
  //   fea14183 4181b3 1c183 fe310323 fe914183 4181b3 1c183 fe3102a3 fe814183 4181b3 1c183 fe310223
  //   ff412183 fe412203 450533 150513 fea12823 fe812e23 1437 40840413 ff014183 3401b3 1c183 ff114203
  //   440233 24203 4181b3 ff214203 440233 24203 4181b3 ff314203 440233 24203 4181b3 1237 40020213 320233
  //   24503 ffc12403 e12223 d12023 1800093 80e7 412703 497b7 6c078793 12683 fee12823 fef12623 fe812e23
  //   fe912c23 1437 30040413 ff014183 340233 100193 320023 fec14183 3401b3 18023 24183 ff114483 940233
  //   100493 920023 fed14483 9404b3 48023 24483 9181b3 ff214483 940233 100493 920023 fee14483 9404b3 48023
  //   24483 9181b3 ff314483 940233 100493 920023 fef14483 9404b3 48023 24483 9181b3 1237 40020213 320233
  //   24203 ff812483 ffc12403 420233 420233 410233 37800193 fe312823 e000193 fe312623 fec22203 20067 49737
  //   67070713 72683 fe012823 14c203 fe4108a3 ff012203 4c503 450533 470713 e12023 fe312a23 fed12423 31237
  //   50020213 feb14183 4181b3 1c183 fe3103a3 fea14183 4181b3 1c183 fe310323 fe914183 4181b3 1c183
  //   fe3102a3 fe814183 4181b3 1c183 fe310223 ff412183 fe412203 450533 150513 fea12823 fe812e23 1437
  //   40840413 ff014183 3401b3 1c183 ff114203 440233 24203 4181b3 ff214203 440233 24203 4181b3 ff314203
  //   440233 24203 4181b3 1237 40020213 320233 24503 ffc12403 1800093 80e7 248493 497b7 6c078793 12703
  //   fe912823 fef12623 fe812e23 fe912c23 1437 30040413 ff014183 340233 100193 320023 fec14183 3401b3
  //   18023 24183 ff114483 940233 100493 920023 fed14483 9404b3 48023 24483 9181b3 ff214483 940233 100493
  //   920023 fee14483 9404b3 48023 24483 9181b3 ff314483 940233 100493 920023 fef14483 9404b3 48023 24483
  //   9181b3 1237 40020213 320233 24203 ff812483 ffc12403 420233 420233 410233 55c00193 fe312823 38000193
  //   fe312623 fec22203 20067 244683 144603 344703 444783 494b7 64048493 8*d686b3 fed12823 fec12623 116b7
  //   60068693 fe012223 ff314203 fe4102a3 fef14203 fe410223 fe412203 468233 24203 fe4105a3 ff214203
  //   fe4102a3 fee14203 fe410223 fe412203 468233 24203 fe410523 ff114203 fe4102a3 fed14203 fe410223
  //   fe412203 468233 24203 fe4104a3 ff014203 fe4102a3 fec14203 fe410223 fe412203 468233 24203 fe410423
  //   fe812683 4a503 fe012823 fee10923 fee12423 fe914203 fe4109a3 ff012703 fee12823 fed12623 11737
  //   60070713 fe012223 ff314203 fe4102a3 fef14203 fe410223 fe412203 470233 24203 fe4105a3 ff214203
  //   fe4102a3 fee14203 fe410223 fe412203 470233 24203 fe410523 ff114203 fe4102a3 fed14203 fe410223
  //   fe412203 470233 24203 fe4104a3 ff014203 fe4102a3 fec14203 fe410223 fe412203 470233 24203 fe410423
  //   fe812703 fe012823 fef109a3 ff012783 fef12823 fee12623 117b7 60078793 fe012223 ff314203 fe4102a3
  //   fef14203 fe410223 fe412203 478233 24203 fe4105a3 ff214203 fe4102a3 fee14203 fe410223 fe412203 478233
  //   24203 fe410523 ff114203 fe4102a3 fed14203 fe410223 fe412203 478233 24203 fe4104a3 ff014203 fe4102a3
  //   fec14203 fe410223 fe412203 478233 24203 fe410423 fe812783 fe312a23 fef12423 31237 50020213 feb14183
  //   4181b3 1c183 fe3103a3 fea14183 4181b3 1c183 fe310323 fe914183 4181b3 1c183 fe3102a3 fe814183 4181b3
  //   1c183 fe310223 ff412183 fe412203 450533 150513 fea12823 fe812e23 1437 40840413 ff014183 3401b3 1c183
  //   ff114203 440233 24203 4181b3 ff214203 440233 24203 4181b3 ff314203 440233 24203 4181b3 1237 400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
endmodule

module ALU (
  input  [31:0] ImmediateNumber32Bit,
  input  [31:0] RegisterData1,
  input  [6:0] SEL,
  input  [2:0] Function3,
  output [31:0] S,
  output [2:0] OperationCode
);

  wire and_1_out, and_2_out, and_3_out, and_4_out, comparator_1_eq, comparator_2_eq, comparator_3_eq,
       comparator_4_eq, comparator_5_eq, comparator_6_eq, comparator_7_eq, comparator_8_eq, comparator_9_eq,
       comparator_10_eq, comparator_11_eq, comparator_12_eq;
  wire [31:0] adder_1_out, adder_2_out, adder_3_out, adder_4_out, adder_5_out, multiplexer_1_out,
       multiplexer_2_out, not_1_out, not_2_out, not_3_out, subtractor_1_out, subtractor_2_out;

  assign not_1_out = ~ImmediateNumber32Bit;  // NOT_Gate not_1, 32 bits wide
  assign not_2_out = ~RegisterData1;  // NOT_Gate not_2, 32 bits wide
  Comparator #(.width(7)) comparator_1 (.a(SEL), .b(7'b0010011), .eq(comparator_1_eq));  // open: gt, lt
  Comparator #(.width(7)) comparator_2 (.a(SEL), .b(7'b1100111), .eq(comparator_2_eq));  // open: gt, lt
  Comparator #(.width(7)) comparator_3 (.a(SEL), .b(7'b0110011), .eq(comparator_3_eq));  // open: gt, lt
  Comparator #(.width(7)) comparator_4 (.a(SEL), .b(7'b0110111), .eq(comparator_4_eq));  // open: gt, lt
  Comparator #(.width(7)) comparator_5 (.a(SEL), .b(7'b0000011), .eq(comparator_5_eq));  // open: gt, lt
  Comparator #(.width(3)) comparator_6 (.a(Function3), .b(3'b010), .eq(comparator_6_eq));  // open: gt, lt
  Comparator #(.width(7)) comparator_7 (.a(SEL), .b(7'b0000011), .eq(comparator_7_eq));  // open: gt, lt
  Comparator #(.width(3)) comparator_8 (.a(Function3), .b(3'b100), .eq(comparator_8_eq));  // open: gt, lt
  Comparator #(.width(7)) comparator_9 (.a(SEL), .b(7'b0100011), .eq(comparator_9_eq));  // open: gt, lt
  Comparator #(.width(3)) comparator_10 (.a(Function3), .b(3'b010), .eq(comparator_10_eq));  // open: gt, lt
  Comparator #(.width(7)) comparator_11 (.a(SEL), .b(7'b0100011), .eq(comparator_11_eq));  // open: gt, lt
  Comparator #(.width(3)) comparator_12 (.a(Function3), .b(3'b000), .eq(comparator_12_eq));  // open: gt, lt
  Adder #(.width(32)) adder_1 (.a(not_1_out), .b(32'h1), .out(adder_1_out));  // open: cin, cout
  Adder #(.width(32)) adder_2 (.a(not_2_out), .b(32'h1), .out(adder_2_out));  // open: cin, cout
  and and_1 (and_1_out, comparator_5_eq, comparator_6_eq);
  and and_2 (and_2_out, comparator_7_eq, comparator_8_eq);
  and and_3 (and_3_out, comparator_9_eq, comparator_10_eq);
  and and_4 (and_4_out, comparator_11_eq, comparator_12_eq);
  Multiplexer #(.width(32)) multiplexer_1 (
    .in0(ImmediateNumber32Bit), .in1(adder_1_out), .out(multiplexer_1_out), .sel(ImmediateNumber32Bit[31]));
  Multiplexer #(.width(32)) multiplexer_2 (
    .in0(RegisterData1), .in1(adder_2_out), .out(multiplexer_2_out), .sel(RegisterData1[31]));
  Priority_Encoder priority_encoder_1 (
    .in0(comparator_1_eq), .in1(comparator_2_eq), .in2(comparator_3_eq), .in3(comparator_4_eq),
    .in4(and_1_out), .in5(and_2_out), .in6(and_3_out), .in7(and_4_out), .out(OperationCode), .en_in(1'b1));  // open: gs, en_out
  Adder #(.width(32)) adder_3 (.a(multiplexer_1_out), .b(multiplexer_2_out), .out(adder_3_out));  // open: cin, cout
  Adder #(.width(32)) adder_4 (.a(multiplexer_1_out), .b(multiplexer_2_out), .out(adder_4_out));  // open: cin, cout
  Subtractor #(.width(32)) subtractor_1 (
    .a(multiplexer_1_out), .b(multiplexer_2_out), .out(subtractor_1_out));  // open: bin, bout
  Subtractor #(.width(32)) subtractor_2 (
    .a(multiplexer_2_out), .b(multiplexer_1_out), .out(subtractor_2_out));  // open: bin, bout
  assign not_3_out = ~adder_3_out;  // NOT_Gate not_3, 32 bits wide
  Adder #(.width(32)) adder_5 (.a(not_3_out), .b(32'h1), .out(adder_5_out));  // open: cin, cout
  Multiplexer #(.select(2), .width(32)) multiplexer_3 (
    .in0(adder_4_out), .in1(subtractor_1_out), .in2(subtractor_2_out), .in3(adder_5_out), .out(S),
    .sel({ImmediateNumber32Bit[31], RegisterData1[31]}));
endmodule

module Extender20_32 (
  input  [19:0] Input20Bit,
  output [31:0] Output32Bit
);


  assign Output32Bit = {Input20Bit, {12{1'b0}}};
endmodule

module Extender12_32 (
  input  [6:0] SEL,
  input  [11:0] Input12Bit,
  output [31:0] Output32Bit
);

  wire comparator_2_eq;
  wire [0:0] multiplexer_1_out, undriven;
  wire [6:0] ADD, LBU, LUI, LW, SB, SW;

  Comparator #(.width(7)) comparator_1 (.a(SEL), .b(7'b0010011));  // open: gt, eq, lt
  Comparator #(.width(7)) comparator_2 (.a(SEL), .b(7'b1100111), .eq(comparator_2_eq));  // open: gt, lt
  Comparator #(.width(7)) comparator_3 (.a(SEL), .b(ADD));  // open: gt, eq, lt
  Comparator #(.width(7)) comparator_4 (.a(SEL), .b(LUI));  // open: gt, eq, lt
  Comparator #(.width(7)) comparator_5 (.a(SEL), .b(LW));  // open: gt, eq, lt
  Comparator #(.width(7)) comparator_6 (.a(SEL), .b(LBU));  // open: gt, eq, lt
  Comparator #(.width(7)) comparator_7 (.a(SEL), .b(SW));  // open: gt, eq, lt
  Comparator #(.width(7)) comparator_8 (.a(SEL), .b(SB));  // open: gt, eq, lt
  assign Output32Bit = {{20{Input12Bit[11]}}, Input12Bit};  // Bit_Extender bit_extender_1
  Multiplexer multiplexer_1 (.in0(undriven[0]), .in1(1'b0), .out(multiplexer_1_out[0]), .sel(comparator_2_eq));
endmodule

module SignAdder (
  input  [31:0] ImmediateNumber32Bit,
  input  [31:0] RegisterData1,
  output [31:0] S
);

  wire [31:0] adder_1_out, adder_2_out, adder_3_out, adder_4_out, adder_5_out, multiplexer_1_out,
       multiplexer_2_out, not_1_out, not_2_out, not_3_out, subtractor_1_out, subtractor_2_out;

  assign not_1_out = ~ImmediateNumber32Bit;  // NOT_Gate not_1, 32 bits wide
  assign not_2_out = ~RegisterData1;  // NOT_Gate not_2, 32 bits wide
  Adder #(.width(32)) adder_1 (.a(not_1_out), .b(32'h1), .out(adder_1_out));  // open: cin, cout
  Adder #(.width(32)) adder_2 (.a(not_2_out), .b(32'h1), .out(adder_2_out));  // open: cin, cout
  Multiplexer #(.width(32)) multiplexer_1 (
    .in0(ImmediateNumber32Bit), .in1(adder_1_out), .out(multiplexer_1_out), .sel(ImmediateNumber32Bit[31]));
  Multiplexer #(.width(32)) multiplexer_2 (
    .in0(RegisterData1), .in1(adder_2_out), .out(multiplexer_2_out), .sel(RegisterData1[31]));
  Adder #(.width(32)) adder_3 (.a(multiplexer_1_out), .b(multiplexer_2_out), .out(adder_3_out));  // open: cin, cout
  Adder #(.width(32)) adder_4 (.a(multiplexer_1_out), .b(multiplexer_2_out), .out(adder_4_out));  // open: cin, cout
  Subtractor #(.width(32)) subtractor_1 (
    .a(multiplexer_1_out), .b(multiplexer_2_out), .out(subtractor_1_out));  // open: bin, bout
  Subtractor #(.width(32)) subtractor_2 (
    .a(multiplexer_2_out), .b(multiplexer_1_out), .out(subtractor_2_out));  // open: bin, bout
  assign not_3_out = ~adder_3_out;  // NOT_Gate not_3, 32 bits wide
  Adder #(.width(32)) adder_5 (.a(not_3_out), .b(32'h1), .out(adder_5_out));  // open: cin, cout
  Multiplexer #(.select(2), .width(32)) multiplexer_3 (
    .in0(adder_4_out), .in1(subtractor_1_out), .in2(subtractor_2_out), .in3(adder_5_out), .out(S),
    .sel({ImmediateNumber32Bit[31], RegisterData1[31]}));
endmodule
