// Logisim project OSOC_F.circ as structural Verilog: 37 circuits, main circuit main
module main (
  input  in_1,
  output out_2
);

  wire clock_1_out;

  Clock clock_1 (.out(clock_1_out));
  D_FF d_ff_1 (.D(in_1), .CLK(clock_1_out), .Q(out_2));
endmodule

module Decoder2_4 (
  input  A1,
  input  A0,
  output Y0,
  output Y1,
  output Y2,
  output Y3
);

  wire not_1_out, not_2_out;

  not not_1 (not_1_out, A1);
  not not_2 (not_2_out, A0);
  and and_1 (Y0, not_1_out, not_2_out);
  and and_2 (Y1, not_1_out, A0);
  and and_3 (Y2, A1, not_2_out);
  and and_4 (Y3, A1, A0);
endmodule

module Decoder3_8 (
  input  A2,
  input  A1,
  input  A0,
  output Y0,
  output Y1,
  output Y2,
  output Y3,
  output Y4,
  output Y5,
  output Y6,
  output Y7
);

  wire decoder2_4_1_y0, decoder2_4_1_y1, decoder2_4_1_y2, decoder2_4_1_y3, decoder2_4_2_y0, decoder2_4_2_y1,
       decoder2_4_2_y2, decoder2_4_2_y3, not_1_out;

  not not_1 (not_1_out, A2);
  Decoder2_4 decoder2_4_1 (
    .A1(A1), .A0(A0), .Y0(decoder2_4_1_y0), .Y1(decoder2_4_1_y1), .Y2(decoder2_4_1_y2), .Y3(decoder2_4_1_y3));
  Decoder2_4 decoder2_4_2 (
    .A1(A1), .A0(A0), .Y0(decoder2_4_2_y0), .Y1(decoder2_4_2_y1), .Y2(decoder2_4_2_y2), .Y3(decoder2_4_2_y3));
  and and_1 (Y0, decoder2_4_1_y0, not_1_out);
  and and_2 (Y1, decoder2_4_1_y1, not_1_out);
  and and_3 (Y2, decoder2_4_1_y2, not_1_out);
  and and_4 (Y3, decoder2_4_1_y3, not_1_out);
  and and_5 (Y4, decoder2_4_2_y0, A2);
  and and_6 (Y5, decoder2_4_2_y1, A2);
  and and_7 (Y6, decoder2_4_2_y2, A2);
  and and_8 (Y7, decoder2_4_2_y3, A2);
endmodule

module LED7 (
  input  A2,
  input  A1,
  input  A0,
  input  Dot_in,
  output A,
  output B,
  output C,
  output D,
  output E,
  output F,
  output G,
  output Dot_out
);

  wire and_1_out, and_2_out, and_3_out, and_4_out, and_5_out, and_6_out, and_7_out, and_8_out, and_9_out,
       and_10_out, and_11_out, and_12_out, and_13_out, and_14_out, and_15_out, and_16_out, not_1_out,
       not_2_out, not_3_out;

  not not_1 (not_1_out, A2);
  not not_2 (not_2_out, A1);
  not not_3 (not_3_out, A0);
  and and_1 (and_1_out, not_1_out, not_3_out);
  and and_2 (and_2_out, A2, A0);
  and and_3 (and_3_out, not_3_out, not_2_out);
  and and_4 (and_4_out, A1, A0);
  and and_5 (and_5_out, A1, not_1_out);
  and and_6 (and_6_out, A1, not_3_out);
  and and_7 (and_7_out, A2, not_2_out, A0);
  and and_8 (and_8_out, not_1_out, not_3_out);
  and and_9 (and_9_out, A1, not_3_out);
  and and_10 (and_10_out, not_1_out, not_3_out);
  and and_11 (and_11_out, not_2_out, not_3_out);
  and and_12 (and_12_out, A2, not_2_out);
  and and_13 (and_13_out, A2, not_3_out);
  and and_14 (and_14_out, A2, not_2_out);
  and and_15 (and_15_out, not_1_out, A1);
  and and_16 (and_16_out, A1, not_3_out);
  or or_1 (A, A1, and_1_out, and_2_out);
  or or_2 (B, not_1_out, and_3_out, and_4_out);
  or or_3 (C, A2, not_2_out, A0);
  or or_4 (D, and_5_out, and_6_out, and_7_out, and_8_out);
  or or_5 (E, and_9_out, and_10_out);
  or or_6 (F, and_11_out, and_12_out, and_13_out);
  or or_7 (G, and_14_out, and_15_out, and_16_out);
  _7_Segment_Display u_7_segment_display_1 (.g(G), .f(F), .a(A), .b(B), .e(E), .d(D), .c(C), .dp(Dot_in));

  assign Dot_out = Dot_in;

  // Other names for the same wires on the sheet: Dot = Dot_in
endmodule

module LED16 (
  input  A3,
  input  A2,
  input  A1,
  input  A0,
  input  Dot_in,
  output E,
  output A,
  output F,
  output B,
  output Dot_out,
  output G,
  output C,
  output D
);

  wire decoder3_8_1_y0, decoder3_8_1_y1, decoder3_8_1_y2, decoder3_8_1_y3, decoder3_8_1_y4, decoder3_8_1_y5,
       decoder3_8_1_y6, decoder3_8_1_y7, decoder3_8_2_y0, decoder3_8_2_y1, decoder3_8_2_y2, decoder3_8_2_y3,
       decoder3_8_2_y4, decoder3_8_2_y5, decoder3_8_2_y6, decoder3_8_2_y7, not_1_out, Y0, Y1, Y2, Y3, Y4, Y5,
       Y6, Y7, Y8, Y9, Ya, Yb, Yc, Yd, Ye, Yf;

  not not_1 (not_1_out, A3);
  Decoder3_8 decoder3_8_1 (
    .A2(A2), .A1(A1), .A0(A0), .Y0(decoder3_8_1_y0), .Y1(decoder3_8_1_y1), .Y2(decoder3_8_1_y2),
    .Y3(decoder3_8_1_y3), .Y4(decoder3_8_1_y4), .Y5(decoder3_8_1_y5), .Y6(decoder3_8_1_y6),
    .Y7(decoder3_8_1_y7));
  Decoder3_8 decoder3_8_2 (
    .A2(A2), .A1(A1), .A0(A0), .Y0(decoder3_8_2_y0), .Y1(decoder3_8_2_y1), .Y2(decoder3_8_2_y2),
    .Y3(decoder3_8_2_y3), .Y4(decoder3_8_2_y4), .Y5(decoder3_8_2_y5), .Y6(decoder3_8_2_y6),
    .Y7(decoder3_8_2_y7));
  and and_1 (Y0, not_1_out, decoder3_8_1_y0);
  and and_2 (Y1, not_1_out, decoder3_8_1_y1);
  and and_3 (Y2, not_1_out, decoder3_8_1_y2);
  and and_4 (Y3, not_1_out, decoder3_8_1_y3);
  and and_5 (Y4, not_1_out, decoder3_8_1_y4);
  and and_6 (Y5, not_1_out, decoder3_8_1_y5);
  and and_7 (Y6, not_1_out, decoder3_8_1_y6);
  and and_8 (Y7, not_1_out, decoder3_8_1_y7);
  and and_9 (Y8, A3, decoder3_8_2_y0);
  and and_10 (Y9, A3, decoder3_8_2_y1);
  and and_11 (Ya, A3, decoder3_8_2_y2);
  and and_12 (Yb, A3, decoder3_8_2_y3);
  and and_13 (Yc, A3, decoder3_8_2_y4);
  and and_14 (Yd, A3, decoder3_8_2_y5);
  and and_15 (Ye, A3, decoder3_8_2_y6);
  and and_16 (Yf, A3, decoder3_8_2_y7);
  or or_1 (A, Y0, Y2, Y3, Y5, Y6, Y7, Y8, Y9, Ya, Yc, Ye, Yf);
  or or_2 (B, Y0, Y1, Y2, Y3, Y4, Y7, Y8, Y9, Ya, Yd);
  or or_3 (C, Y0, Y1, Y3, Y4, Y5, Y6, Y7, Y8, Y9, Ya, Yb, Yd);
  or or_4 (D, Y0, Y2, Y3, Y5, Y6, Y8, Y9, Yb, Yc, Yd, Ye);
  or or_5 (E, Y0, Y2, Y6, Y8, Ya, Yb, Yc, Yd, Ye, Yf);
  or or_6 (F, Y0, Y4, Y5, Y6, Y8, Y9, Ya, Yb, Yc, Ye, Yf);
  or or_7 (G, Y2, Y3, Y4, Y5, Y6, Y8, Y9, Ya, Yb, Yd, Ye, Yf);

  assign Dot_out = Dot_in;
endmodule

module Encoder16_4 (
  input  A0,
  input  A1,
  input  A2,
  input  A3,
  input  A4,
  input  A5,
  input  A6,
  input  A7,
  input  A8,
  input  A9,
  input  A10,
  input  A11,
  input  A12,
  input  A13,
  input  A14,
  input  A15,
  output Y0,
  output Y1,
  output Y2,
  output Y3
);

  or or_1 (Y0, A1, A3, A5, A7, A9, A11, A13, A15);
  or or_2 (Y1, A2, A3, A6, A7, A10, A11, A14, A15);
  or or_3 (Y2, A4, A5, A6, A7, A12, A13, A14, A15);
  or or_4 (Y3, A8, A9, A10, A11, A12, A13, A14, A15);
endmodule

module P_Encoeder4_2 (
  input  A3,
  input  A2,
  input  A1,
  input  A0,
  output Y1,
  output Y0
);

  wire and_1_out, and_2_out, and_3_out, not_1_out, not_2_out;

  not not_1 (not_1_out, A3);
  and and_1 (and_1_out, not_1_out, A2);
  not not_2 (not_2_out, A2);
  and and_2 (and_2_out, not_1_out, not_2_out);
  or or_1 (Y1, A3, and_1_out);
  and and_3 (and_3_out, and_2_out, A1);
  or or_2 (Y0, and_3_out, A3);
endmodule

module P_Encoder16_4 (
  input  Af,
  input  Ae,
  input  Ad,
  input  Ac,
  input  Ab,
  input  Aa,
  input  A9,
  input  A8,
  input  A7,
  input  A6,
  input  A5,
  input  A4,
  input  A3,
  input  A2,
  input  A1,
  input  A0,
  output Y3,
  output Y2,
  output Y1,
  output Y0
);

  wire and_1_out, and_2_out, and_3_out, and_4_out, and_5_out, and_6_out, and_7_out, and_8_out, and_9_out,
       and_10_out, and_11_out, and_12_out, and_13_out, and_14_out, and_15_out, and_16_out, and_17_out,
       and_18_out, and_19_out, and_20_out, and_21_out, and_22_out, and_23_out, and_24_out, and_25_out,
       and_26_out, and_27_out, and_28_out, and_29_out, and_30_out, and_31_out, and_32_out, and_33_out,
       and_34_out, not_1_out, not_2_out, not_3_out, not_4_out, not_5_out, not_6_out, not_7_out, not_8_out,
       not_9_out, not_10_out, not_11_out, not_12_out, not_13_out, not_14_out, not_15_out;

  not not_1 (not_1_out, Af);
  not not_2 (not_2_out, Ae);
  not not_3 (not_3_out, Ad);
  not not_4 (not_4_out, Ac);
  not not_5 (not_5_out, Ab);
  not not_6 (not_6_out, Aa);
  not not_7 (not_7_out, A9);
  not not_8 (not_8_out, A8);
  not not_9 (not_9_out, A7);
  not not_10 (not_10_out, A6);
  not not_11 (not_11_out, A5);
  not not_12 (not_12_out, A4);
  not not_13 (not_13_out, A3);
  not not_14 (not_14_out, A2);
  not not_15 (not_15_out, A1);
  and and_1 (and_1_out, not_1_out, Ae);
  and and_2 (and_2_out, not_1_out, not_2_out);
  and and_3 (and_3_out, not_3_out, not_4_out);
  and and_4 (and_4_out, and_2_out, and_3_out);
  and and_5 (and_5_out, not_5_out, not_6_out);
  and and_6 (and_6_out, not_7_out, not_8_out);
  and and_7 (and_7_out, not_9_out, not_10_out);
  and and_8 (and_8_out, not_11_out, not_12_out);
  and and_9 (and_9_out, not_13_out, not_14_out);
  and and_10 (and_10_out, and_2_out, Ad);
  and and_11 (and_11_out, and_2_out, not_3_out);
  and and_12 (and_12_out, and_11_out, Ac);
  and and_13 (and_13_out, and_4_out, Ab);
  and and_14 (and_14_out, and_4_out, not_5_out);
  and and_15 (and_15_out, and_4_out, and_5_out);
  and and_16 (and_16_out, and_14_out, Aa);
  and and_17 (and_17_out, and_15_out, A9);
  and and_18 (and_18_out, and_15_out, not_7_out);
  and and_19 (and_19_out, and_18_out, A8);
  and and_20 (and_20_out, and_15_out, and_6_out);
  and and_21 (and_21_out, and_20_out, A7);
  and and_22 (and_22_out, and_20_out, not_9_out);
  and and_23 (and_23_out, and_20_out, and_7_out);
  and and_24 (and_24_out, and_22_out, A6);
  and and_25 (and_25_out, and_23_out, A5);
  and and_26 (and_26_out, and_23_out, not_11_out);
  and and_27 (and_27_out, and_23_out, and_8_out);
  and and_28 (and_28_out, and_26_out, A4);
  and and_29 (and_29_out, and_27_out, A3);
  and and_30 (and_30_out, and_27_out, not_13_out);
  and and_31 (and_31_out, and_27_out, and_9_out);
  and and_32 (and_32_out, and_30_out, A2);
  and and_33 (and_33_out, and_31_out, A1);
  and and_34 (and_34_out, and_31_out, not_15_out);
  or or_1 (Y3, Af, and_1_out, and_10_out, and_12_out, and_13_out, and_16_out, and_17_out, and_19_out);
  or or_2 (Y2, Af, and_1_out, and_10_out, and_12_out, and_21_out, and_24_out, and_25_out, and_28_out);
  or or_3 (Y1, Af, and_1_out, and_13_out, and_16_out, and_21_out, and_24_out, and_29_out, and_32_out);
  // AND_Gate and_35 has open pins: in0=and_34_out, in1=A0, out=open
  or or_4 (Y0, Af, and_10_out, and_13_out, and_17_out, and_21_out, and_25_out, and_29_out, and_33_out);
endmodule

module Lead_0 (
  input  [15:0] Lead_0_in,
  output [3:0] Lead_0_Num
);

  wire p_encoder16_4_1_y0, p_encoder16_4_1_y1, p_encoder16_4_1_y2, p_encoder16_4_1_y3;

  P_Encoder16_4 p_encoder16_4_1 (
    .Af(Lead_0_in[15]), .Ae(Lead_0_in[14]), .Ad(Lead_0_in[13]), .Ac(Lead_0_in[12]), .Ab(Lead_0_in[11]),
    .Aa(Lead_0_in[10]), .A9(Lead_0_in[9]), .A8(Lead_0_in[8]), .A7(Lead_0_in[7]), .A6(Lead_0_in[6]),
    .A5(Lead_0_in[5]), .A4(Lead_0_in[4]), .A3(Lead_0_in[3]), .A2(Lead_0_in[2]), .A1(Lead_0_in[1]),
    .A0(Lead_0_in[0]), .Y3(p_encoder16_4_1_y3), .Y2(p_encoder16_4_1_y2), .Y1(p_encoder16_4_1_y1),
    .Y0(p_encoder16_4_1_y0));
  not not_1 (Lead_0_Num[3], p_encoder16_4_1_y3);
  not not_2 (Lead_0_Num[2], p_encoder16_4_1_y2);
  not not_3 (Lead_0_Num[1], p_encoder16_4_1_y1);
  not not_4 (Lead_0_Num[0], p_encoder16_4_1_y0);
endmodule

module Lead_1 (
  input  [15:0] Lead_1_in,
  output [3:0] Lead_1_Num
);

  wire not_1_out, not_2_out, not_3_out, not_4_out, not_5_out, not_6_out, not_7_out, not_8_out, not_9_out,
       not_10_out, not_11_out, not_12_out, not_13_out, not_14_out, not_15_out, not_16_out,
       p_encoder16_4_1_y0, p_encoder16_4_1_y1, p_encoder16_4_1_y2, p_encoder16_4_1_y3;

  not not_1 (not_1_out, Lead_1_in[0]);
  not not_2 (not_2_out, Lead_1_in[1]);
  not not_3 (not_3_out, Lead_1_in[2]);
  not not_4 (not_4_out, Lead_1_in[3]);
  not not_5 (not_5_out, Lead_1_in[4]);
  not not_6 (not_6_out, Lead_1_in[5]);
  not not_7 (not_7_out, Lead_1_in[6]);
  not not_8 (not_8_out, Lead_1_in[7]);
  not not_9 (not_9_out, Lead_1_in[8]);
  not not_10 (not_10_out, Lead_1_in[9]);
  not not_11 (not_11_out, Lead_1_in[10]);
  not not_12 (not_12_out, Lead_1_in[11]);
  not not_13 (not_13_out, Lead_1_in[12]);
  not not_14 (not_14_out, Lead_1_in[13]);
  not not_15 (not_15_out, Lead_1_in[14]);
  not not_16 (not_16_out, Lead_1_in[15]);
  P_Encoder16_4 p_encoder16_4_1 (
    .Af(not_16_out), .Ae(not_15_out), .Ad(not_14_out), .Ac(not_13_out), .Ab(not_12_out), .Aa(not_11_out),
    .A9(not_10_out), .A8(not_9_out), .A7(not_8_out), .A6(not_7_out), .A5(not_6_out), .A4(not_5_out),
    .A3(not_4_out), .A2(not_3_out), .A1(not_2_out), .A0(not_1_out), .Y3(p_encoder16_4_1_y3),
    .Y2(p_encoder16_4_1_y2), .Y1(p_encoder16_4_1_y1), .Y0(p_encoder16_4_1_y0));
  not not_17 (Lead_1_Num[3], p_encoder16_4_1_y3);
  not not_18 (Lead_1_Num[2], p_encoder16_4_1_y2);
  not not_19 (Lead_1_Num[1], p_encoder16_4_1_y1);
  not not_20 (Lead_1_Num[0], p_encoder16_4_1_y0);
endmodule

module Decoder1_2 (
  input  A,
  output Y1,
  output Y0
);

  not not_1 (Y1, A);

  assign Y0 = A;
endmodule

module Mux_3Bit_4_1 (
  input  S1,
  input  S0,
  input  [2:0] D0,
  input  [2:0] D1,
  input  [2:0] D2,
  input  [2:0] D3,
  output [2:0] Y
);

  wire [2:0] and_1_out, and_2_out, and_3_out, and_4_out;
  wire [2:2] decoder2_4_1_y0, decoder2_4_1_y1, decoder2_4_1_y2, decoder2_4_1_y3;

  Decoder2_4 decoder2_4_1 (
    .A1(S1), .A0(S0), .Y0(decoder2_4_1_y0[2]), .Y1(decoder2_4_1_y1[2]), .Y2(decoder2_4_1_y2[2]),
    .Y3(decoder2_4_1_y3[2]));
  assign and_1_out = D0 & {3{decoder2_4_1_y0[2]}};  // AND_Gate and_1, 3 bits wide
  assign and_2_out = D1 & {3{decoder2_4_1_y1[2]}};  // AND_Gate and_2, 3 bits wide
  assign and_3_out = D2 & {3{decoder2_4_1_y2[2]}};  // AND_Gate and_3, 3 bits wide
  assign and_4_out = D3 & {3{decoder2_4_1_y3[2]}};  // AND_Gate and_4, 3 bits wide
  assign Y = and_1_out | and_2_out | and_3_out | and_4_out;  // OR_Gate or_1, 3 bits wide
endmodule

module Mux_1Bit_2_1 (
  input  D0,
  input  D1,
  input  S,
  output Y
);

  wire and_1_out, and_2_out, decoder1_2_1_y0, decoder1_2_1_y1;

  Decoder1_2 decoder1_2_1 (.A(S), .Y1(decoder1_2_1_y1), .Y0(decoder1_2_1_y0));
  and and_1 (and_1_out, D0, decoder1_2_1_y1);
  and and_2 (and_2_out, D1, decoder1_2_1_y0);
  or or_1 (Y, and_1_out, and_2_out);
endmodule

module Switch_LED (
  input  [4:0] in_1
);

  wire A1, A6, and_1_out, and_2_out, and_3_out, and_4_out, and_5_out, and_6_out, and_7_out, and_8_out,
       and_9_out, and_10_out, and_11_out, and_12_out, and_13_out, and_14_out, and_15_out, and_16_out,
       and_17_out, and_18_out, and_19_out, and_20_out, and_21_out, and_22_out, and_23_out, and_24_out,
       and_25_out, and_26_out, and_27_out, and_28_out, and_29_out, and_30_out, and_31_out, and_32_out,
       and_33_out, and_34_out, and_35_out, and_36_out, and_37_out, B1, B6, C1, C6, D1, D6, Dot6, E1, E6, F1,
       F6, G1, G6, led7_1_a, led7_1_b, led7_1_c, led7_1_d, led7_1_e, led7_1_f, led7_1_g, not_1_out,
       not_2_out, not_3_out, not_4_out, not_5_out, not_6_out, not_7_out, not_8_out, not_9_out, not_10_out,
       not_11_out, not_12_out, not_13_out, not_14_out, or_1_out, or_2_out, or_3_out, or_4_out, or_5_out,
       or_6_out, or_7_out, or_8_out, or_9_out, or_10_out, or_11_out, or_12_out, or_13_out, or_14_out,
       or_15_out, or_16_out, or_17_out, or_18_out, or_19_out, or_20_out, or_21_out, or_22_out, or_23_out,
       or_24_out, or_25_out, or_26_out, or_27_out, or_28_out, or_29_out, or_30_out, or_31_out, or_32_out,
       or_33_out, or_34_out, or_35_out, or_36_out, or_37_out, or_38_out, or_39_out, or_40_out, or_41_out,
       or_42_out, or_43_out, or_44_out, or_45_out, or_46_out, or_47_out;

  not not_1 (not_1_out, in_1[0]);
  not not_2 (not_2_out, in_1[1]);
  not not_3 (not_3_out, in_1[1]);
  not not_4 (not_4_out, in_1[0]);
  not not_5 (not_5_out, in_1[2]);
  not not_6 (not_6_out, in_1[2]);
  not not_7 (not_7_out, in_1[0]);
  not not_8 (not_8_out, in_1[2]);
  not not_9 (not_9_out, in_1[1]);
  not not_10 (not_10_out, in_1[0]);
  not not_11 (not_11_out, in_1[1]);
  not not_12 (not_12_out, in_1[2]);
  not not_13 (not_13_out, in_1[4]);
  and and_1 (and_1_out, A6, in_1[4]);
  and and_2 (and_2_out, B6, in_1[4]);
  and and_3 (and_3_out, C6, in_1[4]);
  and and_4 (and_4_out, D6, in_1[4]);
  and and_5 (and_5_out, E6, in_1[4]);
  and and_6 (and_6_out, F6, in_1[4]);
  and and_7 (and_7_out, G6, in_1[4]);
  and and_8 (and_8_out, in_1[2], in_1[1], in_1[0]);
  and and_9 (and_9_out, in_1[2], in_1[1], not_1_out);
  and and_10 (and_10_out, in_1[2], not_2_out, in_1[0]);
  and and_11 (and_11_out, in_1[2], not_3_out, not_4_out);
  and and_12 (and_12_out, not_5_out, in_1[1], in_1[0]);
  and and_13 (and_13_out, not_6_out, in_1[1], not_7_out);
  and and_14 (and_14_out, not_8_out, not_9_out, in_1[0]);
  and and_15 (and_15_out, not_10_out, not_11_out, not_12_out);
  and and_16 (and_16_out, A1, not_13_out);
  and and_17 (and_17_out, B1, not_13_out);
  and and_18 (and_18_out, C1, not_13_out);
  and and_19 (and_19_out, D1, not_13_out);
  and and_20 (and_20_out, E1, not_13_out);
  and and_21 (and_21_out, F1, not_13_out);
  and and_22 (and_22_out, G1, not_13_out);
  LED7 led7_1 (
    .A2(in_1[2]), .A1(in_1[1]), .A0(in_1[0]), .Dot_in(1'b0), .A(led7_1_a), .B(led7_1_b), .C(led7_1_c),
    .D(led7_1_d), .E(led7_1_e), .F(led7_1_f), .G(led7_1_g));  // open: Dot_out
  LED16 led16_1 (
    .A3(in_1[3]), .A2(in_1[2]), .A1(in_1[1]), .A0(in_1[0]), .Dot_in(1'b0), .E(E6), .A(A6), .F(F6), .B(B6),
    .Dot_out(Dot6), .G(G6), .C(C6), .D(D6));
  not not_14 (not_14_out, in_1[3]);
  or or_1 (or_1_out, and_1_out, and_16_out);
  or or_2 (or_2_out, and_2_out, and_17_out);
  or or_3 (or_3_out, and_3_out, and_18_out);
  or or_4 (or_4_out, and_4_out, and_19_out);
  or or_5 (or_5_out, and_5_out, and_20_out);
  or or_6 (or_6_out, and_6_out, and_21_out);
  or or_7 (or_7_out, and_7_out, and_22_out);
  and and_23 (and_23_out, in_1[3], and_8_out);
  and and_24 (and_24_out, in_1[3], and_9_out);
  and and_25 (and_25_out, in_1[3], and_10_out);
  and and_26 (and_26_out, in_1[3], and_11_out);
  and and_27 (and_27_out, in_1[3], and_12_out);
  and and_28 (and_28_out, in_1[3], and_13_out);
  and and_29 (and_29_out, and_14_out, in_1[3]);
  and and_30 (and_30_out, and_15_out, in_1[3]);
  and and_31 (and_31_out, led7_1_a, not_14_out);
  and and_32 (and_32_out, led7_1_b, not_14_out);
  and and_33 (and_33_out, led7_1_c, not_14_out);
  and and_34 (and_34_out, led7_1_d, not_14_out);
  and and_35 (and_35_out, led7_1_e, not_14_out);
  and and_36 (and_36_out, led7_1_f, not_14_out);
  and and_37 (and_37_out, led7_1_g, not_14_out);
  _7_Segment_Display u_7_segment_display_1 (
    .g(or_7_out), .f(or_6_out), .a(or_1_out), .b(or_2_out), .e(or_5_out), .d(or_4_out), .c(or_3_out));  // open: dp
  or or_8 (or_8_out, and_24_out, 1'b0);
  or or_9 (or_9_out, 1'b0, and_23_out);
  or or_10 (or_10_out, and_24_out, 1'b0);
  or or_11 (or_11_out, and_24_out, and_23_out);
  or or_12 (or_12_out, and_24_out, and_23_out);
  or or_13 (or_13_out, and_25_out, 1'b0);
  or or_14 (or_14_out, 1'b0, or_8_out);
  or or_15 (or_15_out, 1'b0, or_9_out);
  or or_16 (or_16_out, and_25_out, 1'b0);
  or or_17 (or_17_out, 1'b0, or_10_out);
  or or_18 (or_18_out, 1'b0, or_11_out);
  or or_19 (or_19_out, and_25_out, or_12_out);
  or or_20 (or_20_out, and_26_out, or_13_out);
  or or_21 (or_21_out, 1'b0, or_14_out);
  or or_22 (or_22_out, 1'b0, or_15_out);
  or or_23 (or_23_out, and_26_out, or_16_out);
  or or_24 (or_24_out, 1'b0, or_17_out);
  or or_25 (or_25_out, 1'b0, or_18_out);
  or or_26 (or_26_out, and_27_out, or_19_out);
  or or_27 (or_27_out, 1'b0, or_20_out);
  or or_28 (or_28_out, and_28_out, or_21_out);
  or or_29 (or_29_out, and_28_out, or_22_out);
  or or_30 (or_30_out, 1'b0, or_23_out);
  or or_31 (or_31_out, 1'b0, or_24_out);
  or or_32 (or_32_out, 1'b0, or_25_out);
  or or_33 (or_33_out, and_28_out, or_26_out);
  or or_34 (or_34_out, or_27_out, and_29_out);
  or or_35 (or_35_out, or_28_out, and_29_out);
  or or_36 (or_36_out, or_29_out, and_29_out);
  or or_37 (or_37_out, or_30_out, and_29_out);
  or or_38 (or_38_out, or_31_out, 1'b0);
  or or_39 (or_39_out, or_32_out, and_29_out);
  or or_40 (or_40_out, or_33_out, and_29_out);
  or or_41 (or_41_out, or_34_out, and_30_out);
  or or_42 (or_42_out, or_35_out, and_30_out);
  or or_43 (or_43_out, or_36_out, and_30_out);
  or or_44 (or_44_out, or_37_out, and_30_out);
  or or_45 (or_45_out, or_38_out, and_30_out);
  or or_46 (or_46_out, or_39_out, and_30_out);
  or or_47 (or_47_out, or_40_out, and_30_out);
  or or_48 (A1, or_41_out, and_31_out);
  or or_49 (B1, or_42_out, and_32_out);
  or or_50 (C1, or_43_out, and_33_out);
  or or_51 (D1, or_44_out, and_34_out);
  or or_52 (E1, or_45_out, and_35_out);
  or or_53 (F1, or_46_out, and_36_out);
  or or_54 (G1, or_47_out, and_37_out);
endmodule

module Compare_4Bit (
  input  A0,
  input  B0,
  input  A1,
  input  B1,
  input  A2,
  input  B2,
  input  A3,
  input  B3,
  output Y
);

  wire not_1_out, not_2_out, not_3_out, not_4_out, xor_1_out, xor_2_out, xor_3_out, xor_4_out;

  xor xor_1 (xor_1_out, A0, B0);
  xor xor_2 (xor_2_out, A1, B1);
  xor xor_3 (xor_3_out, A2, B2);
  xor xor_4 (xor_4_out, A3, B3);
  not not_1 (not_1_out, xor_1_out);
  not not_2 (not_2_out, xor_2_out);
  not not_3 (not_3_out, xor_3_out);
  not not_4 (not_4_out, xor_4_out);
  and and_1 (Y, not_1_out, not_2_out, not_3_out, not_4_out);
  LED led_1 (.in(Y));
endmodule

module FA_1Bit (
  input  Cin,
  input  A,
  input  B,
  output Cout,
  output S
);

  wire and_1_out, and_2_out, not_1_out, or_1_out;

  not not_1 (not_1_out, Cin);
  and and_1 (and_1_out, A, not_1_out, B);
  or or_1 (or_1_out, A, B);
  and and_2 (and_2_out, or_1_out, Cin);
  xor xor_1 (S, A, Cin, B);
  or or_2 (Cout, and_1_out, and_2_out);
endmodule

module FA_1Bit_From_HA (
  input  Cin,
  input  A,
  input  B,
  output Cout,
  output S
);

  wire ha_1bit_1_cout, ha_1bit_1_s, ha_1bit_2_cout;

  HA_1Bit ha_1bit_1 (.A(A), .B(B), .Cout(ha_1bit_1_cout), .S(ha_1bit_1_s));
  HA_1Bit ha_1bit_2 (.A(Cin), .B(ha_1bit_1_s), .Cout(ha_1bit_2_cout), .S(S));
  or or_1 (Cout, ha_1bit_1_cout, ha_1bit_2_cout);
endmodule

module HA_1Bit (
  input  A,
  input  B,
  output Cout,
  output S
);

  and and_1 (Cout, A, B);
  xor xor_1 (S, A, B);
endmodule

module FA_4Bit (
  input  Cin,
  input  A0,
  input  A1,
  input  A2,
  input  A3,
  input  B0,
  input  B1,
  input  B2,
  input  B3,
  output Cout,
  output S0,
  output S1,
  output S2,
  output S3
);

  wire fa_1bit_1_cout, fa_1bit_2_cout, fa_1bit_3_cout;

  FA_1Bit fa_1bit_1 (.Cin(Cin), .A(A0), .B(B0), .Cout(fa_1bit_1_cout), .S(S0));
  FA_1Bit fa_1bit_2 (.Cin(fa_1bit_1_cout), .A(A1), .B(B1), .Cout(fa_1bit_2_cout), .S(S1));
  FA_1Bit fa_1bit_3 (.Cin(fa_1bit_2_cout), .A(A2), .B(B2), .Cout(fa_1bit_3_cout), .S(S2));
  FA_1Bit fa_1bit_4 (.Cin(fa_1bit_3_cout), .A(A3), .B(B3), .Cout(Cout), .S(S3));
endmodule

module Subtraction_4Bit (
  input  Cin,
  input  A0,
  input  B0,
  input  A1,
  input  B1,
  input  A2,
  input  B2,
  input  A3,
  input  B3,
  output Cout,
  output S0,
  output S1,
  output S2,
  output S3
);

  wire fullsubstraction_1bit_1_cout, fullsubstraction_1bit_2_cout, fullsubstraction_1bit_3_cout;

  LED led_1 (.in(Cout));
  FullSubstraction_1Bit fullsubstraction_1bit_1 (
    .Cin(Cin), .A(A0), .B(B0), .Cout(fullsubstraction_1bit_1_cout), .S(S0));
  FullSubstraction_1Bit fullsubstraction_1bit_2 (
    .Cin(fullsubstraction_1bit_1_cout), .A(A1), .B(B1), .Cout(fullsubstraction_1bit_2_cout), .S(S1));
  FullSubstraction_1Bit fullsubstraction_1bit_3 (
    .Cin(fullsubstraction_1bit_2_cout), .A(A2), .B(B2), .Cout(fullsubstraction_1bit_3_cout), .S(S2));
  FullSubstraction_1Bit fullsubstraction_1bit_4 (
    .Cin(fullsubstraction_1bit_3_cout), .A(A3), .B(B3), .Cout(Cout), .S(S3));
endmodule

module FullSubstraction_1Bit (
  input  Cin,
  input  A,
  input  B,
  output Cout,
  output S
);

  wire and_1_out, and_2_out, and_3_out, not_1_out;

  not not_1 (not_1_out, A);
  xor xor_1 (S, Cin, A, B);
  and and_1 (and_1_out, not_1_out, B);
  and and_2 (and_2_out, not_1_out, Cin);
  and and_3 (and_3_out, B, Cin);
  or or_1 (Cout, and_1_out, and_2_out, and_3_out);
endmodule

module Ones_Comp_4Bit (
  input  A3,
  input  A2,
  input  A1,
  input  A0,
  input  B3,
  input  B2,
  input  B1,
  input  B0,
  output [3:0] out_9,
  output [3:0] Result
);

  wire adder_1_cout;

  Adder #(.width(4)) adder_1 (.a({A3, A2, A1, A0}), .b({B3, B2, B1, B0}), .out(out_9), .cin(1'b0), .cout(adder_1_cout));
  Adder #(.width(4)) adder_2 (.a(out_9), .b(4'b0000), .out(Result), .cin(adder_1_cout));  // open: cout
endmodule

module Origin_Adder (
  input  A3,
  input  A2,
  input  A1,
  input  A0,
  input  B3,
  input  B2,
  input  B1,
  input  B0,
  output [3:0] Result
);

  wire and_1_out, and_2_out, and_3_out, and_4_out, and_5_out, led16_1_a, led16_1_b, led16_1_c, led16_1_d,
       led16_1_dot_out, led16_1_e, led16_1_f, led16_1_g, not_1_out, not_2_out, not_3_out, or_1_out,
       subtractor_1_bout, xor_1_out;
  wire [2:0] adder_1_out, multiplexer_1_out, subtractor_1_out, subtractor_2_out;
  wire [3:3] adder_1_cout;

  xor xor_1 (xor_1_out, A3, B3);
  Adder #(.width(3)) adder_1 (
    .a({A2, A1, A0}), .b({B2, B1, B0}), .out(adder_1_out), .cout(adder_1_cout[3]));  // open: cin
  Subtractor #(.width(3)) subtractor_1 (
    .a({A2, A1, A0}), .b({B2, B1, B0}), .out(subtractor_1_out), .bin(1'b0), .bout(subtractor_1_bout));
  Subtractor #(.width(3)) subtractor_2 (
    .a({B2, B1, B0}), .b({A2, A1, A0}), .out(subtractor_2_out), .bin(1'b0));  // open: bout
  not not_1 (not_1_out, B3);
  not not_2 (not_2_out, A3);
  Multiplexer #(.width(3)) multiplexer_1 (
    .in0(subtractor_1_out), .in1(subtractor_2_out), .out(multiplexer_1_out), .sel(subtractor_1_bout));
  and and_1 (and_1_out, A3, B3);
  and and_2 (and_2_out, A3, not_1_out);
  and and_3 (and_3_out, not_2_out, B3);
  Multiplexer #(.width(4)) multiplexer_2 (
    .in0({adder_1_cout[3], adder_1_out}), .in1({1'b0, multiplexer_1_out}), .out(Result), .sel(xor_1_out));
  and and_4 (and_4_out, and_2_out, not_3_out);
  not not_3 (not_3_out, subtractor_1_bout);
  and and_5 (and_5_out, and_3_out, subtractor_1_bout);
  or or_1 (or_1_out, and_1_out, and_4_out, and_5_out);
  _7_Segment_Display u_7_segment_display_1 (.g(or_1_out));  // open: f, a, b, e, d, c, dp
  LED16 led16_1 (
    .A3(Result[3]), .A2(Result[2]), .A1(Result[1]), .A0(Result[0]), .Dot_in(1'b0), .E(led16_1_e),
    .A(led16_1_a), .F(led16_1_f), .B(led16_1_b), .Dot_out(led16_1_dot_out), .G(led16_1_g), .C(led16_1_c),
    .D(led16_1_d));
  _7_Segment_Display u_7_segment_display_2 (
    .g(led16_1_g), .f(led16_1_f), .a(led16_1_a), .b(led16_1_b), .e(led16_1_e), .d(led16_1_d), .c(led16_1_c),
    .dp(led16_1_dot_out));
endmodule

module SR_Latch (
  input  R,
  input  S,
  output Q,
  output Q_not
);

  nor nor_1 (Q, R, Q_not);
  nor nor_2 (Q_not, Q, S);
endmodule

module SR_Latch_NAND (
  input  S_Not,
  input  R_Not,
  output Q,
  output Q_Not
);

  nand nand_1 (Q, S_Not, Q_Not);
  nand nand_2 (Q_Not, Q, R_Not);
endmodule

module D_Latch (
  input  WE,
  input  D,
  output Q,
  output Q_Not
);

  wire and_1_out, and_2_out, not_1_out;

  not not_1 (not_1_out, D);
  and and_1 (and_1_out, not_1_out, WE);
  and and_2 (and_2_out, WE, D);
  nor nor_1 (Q, and_1_out, Q_Not);
  nor nor_2 (Q_Not, Q, and_2_out);
endmodule

module D_Latch_Reset (
  input  WE,
  input  R,
  input  D,
  output Q,
  output Q_Not
);

  wire multiplexer_1_out;

  Multiplexer multiplexer_1 (.in0(D), .in1(1'b0), .out(multiplexer_1_out), .sel(R));
  D_Latch d_latch_1 (.WE(WE), .D(multiplexer_1_out), .Q(Q), .Q_Not(Q_Not));
endmodule

module D_Osci (
  input  WE,
  output Q
);

  wire d_latch_1_q_not;

  D_Latch d_latch_1 (.WE(WE), .D(d_latch_1_q_not), .Q(Q), .Q_Not(d_latch_1_q_not));
endmodule

module D_FF (
  input  D,
  input  CLK,
  output Q
);

  wire d_latch_1_q, not_1_out;

  not not_1 (not_1_out, CLK);
  D_Latch d_latch_1 (.WE(not_1_out), .D(D), .Q(d_latch_1_q));  // open: Q_Not
  D_Latch d_latch_2 (.WE(D), .D(d_latch_1_q), .Q(Q));  // open: Q_Not
endmodule

module D_FF_Reset (
  input  D,
  input  Reset,
  input  CLK,
  output Q
);

  wire d_latch_reset_1_q, not_1_out;

  not not_1 (not_1_out, CLK);
  D_Latch_Reset d_latch_reset_1 (.WE(not_1_out), .R(Reset), .D(D), .Q(d_latch_reset_1_q));  // open: Q_Not
  D_Latch_Reset d_latch_reset_2 (.WE(CLK), .R(Reset), .D(d_latch_reset_1_q), .Q(Q));  // open: Q_Not
endmodule

module D_FF_Osci (
  input  reset,
  output Q
);

  wire clk_out, not_1_out;

  Clock clk (.out(clk_out));
  not not_1 (not_1_out, Q);
  D_FF_Reset d_ff_reset_1 (.D(not_1_out), .Reset(reset), .CLK(clk_out), .Q(Q));
endmodule

module D_FF_neg (
  input  D,
  input  CLK,
  output Q
);

  wire d_latch_1_q, not_1_out;

  not not_1 (not_1_out, CLK);
  D_Latch d_latch_1 (.WE(CLK), .D(D), .Q(d_latch_1_q));  // open: Q_Not
  D_Latch d_latch_2 (.WE(not_1_out), .D(d_latch_1_q), .Q(Q));  // open: Q_Not
endmodule

module D_FF_EN (
  input  D,
  input  EN,
  input  clk,
  output Q,
  output Q_Not
);

  wire and_1_out;

  and and_1 (and_1_out, EN, clk);
  D_Flip_Flop d_ff_1 (.D(D), .clk(and_1_out), .Q(Q), .Qn(Q_Not));  // open: preset, reset
endmodule

module Reg_4 (
  input  EN,
  input  CLK,
  input  D0,
  input  D1,
  input  D2,
  input  D3,
  output Q0,
  output Q1,
  output Q2,
  output Q3
);

  D_FF_EN d_ff_en_1 (.D(D0), .EN(EN), .clk(CLK), .Q(Q0));  // open: Q_Not
  D_FF_EN d_ff_en_2 (.D(D1), .EN(EN), .clk(CLK), .Q(Q1));  // open: Q_Not
  D_FF_EN d_ff_en_3 (.D(D2), .EN(EN), .clk(CLK), .Q(Q2));  // open: Q_Not
  D_FF_EN d_ff_en_4 (.D(D3), .EN(EN), .clk(CLK), .Q(Q3));  // open: Q_Not
endmodule

module Counter_4Bit (
  input  EN,
  input  CLK
);

  wire adder_1_cout, adder_1_out, adder_2_cout, adder_2_out, adder_3_cout, adder_3_out, adder_4_out,
       reg_4_1_q0, reg_4_1_q1, reg_4_1_q2, reg_4_1_q3;

  Reg_4 reg_4_1 (
    .EN(EN), .CLK(CLK), .D0(adder_1_out), .D1(adder_2_out), .D2(adder_3_out), .D3(adder_4_out),
    .Q0(reg_4_1_q0), .Q1(reg_4_1_q1), .Q2(reg_4_1_q2), .Q3(reg_4_1_q3));
  Adder #(.width(1)) adder_1 (.a(reg_4_1_q0), .b(1'b1), .out(adder_1_out), .cin(1'b0), .cout(adder_1_cout));
  Adder #(.width(1)) adder_2 (.a(reg_4_1_q1), .b(1'b0), .out(adder_2_out), .cin(adder_1_cout), .cout(adder_2_cout));
  Adder #(.width(1)) adder_3 (.a(reg_4_1_q2), .b(1'b0), .out(adder_3_out), .cin(adder_2_cout), .cout(adder_3_cout));
  Adder #(.width(1)) adder_4 (.a(reg_4_1_q3), .b(1'b0), .out(adder_4_out), .cin(adder_3_cout));  // open: cout
endmodule

module Seq_Adder (
  input  EN,
  input  CLK,
  output [7:0] Sum
);

  wire adder_2_cout, adder_3_cout, adder_4_cout, and_1_out, and_2_out, and_3_out, d_ff_1_q, d_ff_2_q,
       not_1_out, not_2_out;
  wire [3:0] adder_2_out, multiplexer_1_out, reg_4_1_q0;
  wire [7:0] adder_1_out;

  Register register_1 (.D(adder_1_out), .en(EN), .clk(CLK), .Q(Sum), .clr(d_ff_2_q));
  Adder adder_1 (.a(Sum), .b({4'b0000, reg_4_1_q0}), .out(adder_1_out));  // open: cin, cout
  Reg_4 reg_4_1 (
    .EN(EN), .CLK(CLK), .D0(multiplexer_1_out[0]), .D1(multiplexer_1_out[1]), .D2(multiplexer_1_out[2]),
    .D3(multiplexer_1_out[3]), .Q0(reg_4_1_q0[0]), .Q1(reg_4_1_q0[1]), .Q2(reg_4_1_q0[2]), .Q3(reg_4_1_q0[3]));
  Multiplexer #(.width(4)) multiplexer_1 (.in0(adder_2_out), .in1(4'b0000), .out(multiplexer_1_out), .sel(and_2_out));
  not not_1 (not_1_out, reg_4_1_q0[0]);
  not not_2 (not_2_out, reg_4_1_q0[2]);
  Adder #(.width(1)) adder_2 (.a(reg_4_1_q0[0]), .b(1'b1), .out(adder_2_out[0]), .cin(1'b0), .cout(adder_2_cout));
  Adder #(.width(1)) adder_3 (
    .a(reg_4_1_q0[1]), .b(1'b0), .out(adder_2_out[1]), .cin(adder_2_cout), .cout(adder_3_cout));
  Adder #(.width(1)) adder_4 (
    .a(reg_4_1_q0[2]), .b(1'b0), .out(adder_2_out[2]), .cin(adder_3_cout), .cout(adder_4_cout));
  Adder #(.width(1)) adder_5 (.a(reg_4_1_q0[3]), .b(1'b0), .out(adder_2_out[3]), .cin(adder_4_cout));  // open: cout
  and and_1 (and_1_out, not_1_out, reg_4_1_q0[1]);
  and and_2 (and_2_out, and_1_out, and_3_out);
  and and_3 (and_3_out, not_2_out, reg_4_1_q0[3]);
  D_Flip_Flop d_ff_1 (.D(and_2_out), .clk(CLK), .Q(d_ff_1_q));  // open: Qn, preset, reset
  D_Flip_Flop d_ff_2 (.D(d_ff_1_q), .clk(CLK), .Q(d_ff_2_q));  // open: Qn, preset, reset
endmodule

module Digital_Clock (
  input  in_1,
  input  in_2
);

  wire comparator_1_eq, comparator_2_eq, d_ff_1_q, d_ff_2_q, led16_1_a, led16_1_b, led16_1_c, led16_1_d,
       led16_1_dot_out, led16_1_e, led16_1_f, led16_1_g, led16_2_a, led16_2_b, led16_2_c, led16_2_d,
       led16_2_dot_out, led16_2_e, led16_2_f, led16_2_g, led16_3_a, led16_3_b, led16_3_c, led16_3_d,
       led16_3_dot_out, led16_3_e, led16_3_f, led16_3_g, led16_4_a, led16_4_b, led16_4_c, led16_4_d,
       led16_4_dot_out, led16_4_e, led16_4_f, led16_4_g;
  wire [3:0] undriven, undriven_2, undriven_3, undriven_4;
  wire [5:0] adder_1_out, adder_2_out, register_1_q, register_2_q;

  LED16 led16_1 (
    .A3(undriven[3]), .A2(undriven[2]), .A1(undriven[1]), .A0(undriven[0]), .E(led16_1_e), .A(led16_1_a),
    .F(led16_1_f), .B(led16_1_b), .Dot_out(led16_1_dot_out), .G(led16_1_g), .C(led16_1_c), .D(led16_1_d));  // open: Dot_in
  LED16 led16_2 (
    .A3(undriven_2[3]), .A2(undriven_2[2]), .A1(undriven_2[1]), .A0(undriven_2[0]), .E(led16_2_e),
    .A(led16_2_a), .F(led16_2_f), .B(led16_2_b), .Dot_out(led16_2_dot_out), .G(led16_2_g), .C(led16_2_c),
    .D(led16_2_d));  // open: Dot_in
  Register #(.width(6)) register_1 (.D(adder_1_out), .clk(in_1), .Q(register_1_q), .clr(d_ff_1_q));  // open: en
  Register #(.width(6)) register_2 (.D(adder_2_out), .clk(in_2), .Q(register_2_q), .clr(d_ff_2_q));  // open: en
  _7_Segment_Display u_7_segment_display_1 (
    .g(led16_1_g), .f(led16_1_f), .a(led16_1_a), .b(led16_1_b), .e(led16_1_e), .d(led16_1_d), .c(led16_1_c),
    .dp(led16_1_dot_out));
  _7_Segment_Display u_7_segment_display_2 (
    .g(led16_2_g), .f(led16_2_f), .a(led16_2_a), .b(led16_2_b), .e(led16_2_e), .d(led16_2_d), .c(led16_2_c),
    .dp(led16_2_dot_out));
  Adder #(.width(6)) adder_1 (.a(register_1_q), .b(6'b000001), .out(adder_1_out));  // open: cin, cout
  Adder #(.width(6)) adder_2 (.a(register_2_q), .b(6'b000001), .out(adder_2_out));  // open: cin, cout
  D_Flip_Flop d_ff_1 (.D(comparator_1_eq), .clk(in_1), .Q(d_ff_1_q));  // open: Qn, preset, reset
  Comparator #(.width(6)) comparator_1 (.a(6'b111011), .b(adder_1_out), .eq(comparator_1_eq));  // open: gt, lt
  D_Flip_Flop d_ff_2 (.D(comparator_2_eq), .clk(in_2), .Q(d_ff_2_q));  // open: Qn, preset, reset
  Comparator #(.width(6)) comparator_2 (.a(6'b111011), .b(adder_2_out), .eq(comparator_2_eq));  // open: gt, lt
  LED16 led16_3 (
    .A3(undriven_3[3]), .A2(undriven_3[2]), .A1(undriven_3[1]), .A0(undriven_3[0]), .E(led16_3_e),
    .A(led16_3_a), .F(led16_3_f), .B(led16_3_b), .Dot_out(led16_3_dot_out), .G(led16_3_g), .C(led16_3_c),
    .D(led16_3_d));  // open: Dot_in
  LED16 led16_4 (
    .A3(undriven_4[3]), .A2(undriven_4[2]), .A1(undriven_4[1]), .A0(undriven_4[0]), .E(led16_4_e),
    .A(led16_4_a), .F(led16_4_f), .B(led16_4_b), .Dot_out(led16_4_dot_out), .G(led16_4_g), .C(led16_4_c),
    .D(led16_4_d));  // open: Dot_in
  _7_Segment_Display u_7_segment_display_3 (
    .g(led16_3_g), .f(led16_3_f), .a(led16_3_a), .b(led16_3_b), .e(led16_3_e), .d(led16_3_d), .c(led16_3_c),
    .dp(led16_3_dot_out));
  _7_Segment_Display u_7_segment_display_4 (
    .g(led16_4_g), .f(led16_4_f), .a(led16_4_a), .b(led16_4_b), .e(led16_4_e), .d(led16_4_d), .c(led16_4_c),
    .dp(led16_4_dot_out));
endmodule
